// Logisim project 2-13.circ as structural Verilog
module _2_13_a (
  input  x,
  input  y,
  input  z,
  input  u,
  output F
);

  wire not_1_out, not_2_out, not_3_out, not_4_out, or_1_out, or_2_out;

  not not_1 (not_1_out, x);
  not not_2 (not_2_out, y);
  not not_3 (not_3_out, z);
  not not_4 (not_4_out, u);
  or or_1 (or_1_out, u, not_1_out);
  or or_2 (or_2_out, not_2_out, z);
  and and_1 (F, or_1_out, or_2_out);

  // Notes on the sheet:
  //   F = (u + x')(y' + z)
  //   u + x'
  //   y' + z
endmodule

module _2_13_b (
  input  x,
  input  y,
  input  u,
  output F
);

  wire not_1_out, not_2_out, not_3_out, xnor_1_out;

  not not_1 (not_1_out, x);
  not not_2 (not_2_out, y);
  not not_3 (not_3_out, u);
  xnor xnor_1 (xnor_1_out, u, y);
  or or_1 (F, xnor_1_out, x);

  // Notes on the sheet:
  //   F = (u XOR y)' + x
  //   u XOR y
endmodule

module _2_13_c (
  input  x,
  input  y,
  input  z,
  input  u,
  output F
);

  wire not_1_out, not_2_out, not_3_out, not_4_out, or_1_out, or_2_out;

  not not_1 (not_1_out, x);
  not not_2 (not_2_out, y);
  not not_3 (not_3_out, z);
  not not_4 (not_4_out, u);
  or or_1 (or_1_out, not_4_out, not_1_out);
  or or_2 (or_2_out, y, not_3_out);
  and and_1 (F, or_1_out, or_2_out);

  // Notes on the sheet:
  //   F = (u' + x')(y + z')
  //   u' + x'
  //   y + z'
endmodule

module _2_13_d (
  input  x,
  input  y,
  input  z,
  input  u,
  output F
);

  wire and_1_out, not_1_out, not_2_out, not_3_out, not_4_out, xor_1_out;

  not not_1 (not_1_out, x);
  not not_2 (not_2_out, y);
  not not_3 (not_3_out, z);
  not not_4 (not_4_out, u);
  xor xor_1 (xor_1_out, x, z);
  and and_1 (and_1_out, xor_1_out, u);
  or or_1 (F, and_1_out, not_2_out);

  // Notes on the sheet:
  //   F = u(x XOR z) + y'
  //   x XOR z
endmodule

module _2_13_e (
  input  x,
  input  y,
  input  z,
  input  u,
  output F
);

  wire and_1_out, and_2_out, not_1_out, not_2_out, not_3_out, not_4_out;

  not not_1 (not_1_out, x);
  not not_2 (not_2_out, y);
  not not_3 (not_3_out, z);
  not not_4 (not_4_out, u);
  and and_1 (and_1_out, y, z);
  and and_2 (and_2_out, u, x, y);
  or or_1 (F, and_1_out, and_2_out, u);

  // Notes on the sheet:
  //   F = u + yz + uxy
  //   yz
  //   uxy
endmodule

module _2_13_f (
  input  x,
  input  y,
  input  u,
  output F
);

  wire and_1_out, not_1_out, not_2_out, not_3_out, or_1_out;

  not not_1 (not_1_out, x);
  not not_2 (not_2_out, y);
  not not_3 (not_3_out, u);
  or or_1 (or_1_out, u, not_2_out);
  and and_1 (and_1_out, or_1_out, not_1_out);
  or or_2 (F, and_1_out, u, x);

  // Notes on the sheet:
  //   F = u + x + x'(u + y')
  //   u + y'
endmodule
