// Logisim project 2-14.circ as structural Verilog
module _2_14_a (
  input  x,
  input  y,
  input  z,
  output F
);

  wire and_1_out, and_2_out, and_3_out, not_1_out, not_2_out, not_3_out;

  not not_1 (not_1_out, x);
  not not_2 (not_2_out, y);
  not not_3 (not_3_out, z);
  and and_1 (and_1_out, x, y);
  and and_2 (and_2_out, not_1_out, not_2_out);
  and and_3 (and_3_out, not_2_out, z);
  or or_1 (F, and_1_out, and_2_out, and_3_out);

  // Notes on the sheet:
  //   F = xy + x'y' + y'z
endmodule

module _2_14_b (
  input  x,
  input  y,
  input  z,
  output F
);

  wire not_1_out, not_2_out, not_3_out, not_4_out, not_5_out, not_6_out, or_1_out, or_2_out, or_3_out;

  not not_1 (not_1_out, x);
  not not_2 (not_2_out, y);
  not not_3 (not_3_out, z);
  or or_1 (or_1_out, not_1_out, not_2_out);
  not not_4 (not_4_out, or_1_out);
  or or_2 (or_2_out, x, y);
  not not_5 (not_5_out, or_2_out);
  or or_3 (or_3_out, y, not_3_out);
  not not_6 (not_6_out, or_3_out);
  or or_4 (F, not_4_out, not_5_out, not_6_out);

  // Notes on the sheet:
  //   Using OR Gate and intverter
  //   F = (x' + y')' + (x + y)' + (y + z')'
endmodule

module _2_14_c (
  input  x,
  input  y,
  input  z,
  output F
);

  wire and_1_out, and_2_out, and_3_out, and_4_out, not_1_out, not_2_out, not_3_out, not_4_out, not_5_out,
       not_6_out;

  not not_1 (not_1_out, x);
  not not_2 (not_2_out, y);
  not not_3 (not_3_out, z);
  and and_1 (and_1_out, x, y);
  and and_2 (and_2_out, not_1_out, not_2_out);
  and and_3 (and_3_out, not_2_out, z);
  not not_4 (not_4_out, and_1_out);
  not not_5 (not_5_out, and_2_out);
  not not_6 (not_6_out, and_3_out);
  not not_7 (F, and_4_out);
  and and_4 (and_4_out, not_4_out, not_6_out);

  // Notes on the sheet:
  //   F = ((xy)'(x'y')'(y'z)')'
  //   Using AND Gate and intverter
endmodule

module _2_14_d (
  input  x,
  input  y,
  input  z,
  output F
);

  wire nand_1_out, nand_2_out, nand_3_out, not_1_out, not_2_out, not_3_out;

  not not_1 (not_1_out, x);
  not not_2 (not_2_out, y);
  not not_3 (not_3_out, z);
  nand nand_1 (nand_1_out, x, y);
  nand nand_2 (nand_2_out, not_1_out, not_2_out);
  nand nand_3 (nand_3_out, not_2_out, z);
  nand nand_4 (F, nand_1_out, nand_2_out, nand_3_out);

  // Notes on the sheet:
  //   F = ((xy)'(x'y')'(y'z)')'
  //   Using NAND Gate and intverter
endmodule

module _2_14_e (
  input  x,
  input  y,
  input  z,
  output F
);

  wire nor_1_out, nor_2_out, nor_3_out, nor_4_out, not_1_out, not_2_out, not_3_out;

  not not_1 (not_1_out, x);
  not not_2 (not_2_out, y);
  not not_3 (not_3_out, z);
  nor nor_1 (nor_1_out, not_1_out, not_2_out);
  nor nor_2 (nor_2_out, x, y);
  nor nor_3 (nor_3_out, y, not_3_out);
  nor nor_4 (nor_4_out, nor_1_out, nor_2_out, nor_3_out);
  not not_4 (F, nor_4_out);

  // Notes on the sheet:
  //   Using NOR Gate and intverter
  //   F = (((x' + y')' + (x + y)' + (y + z')')')'
endmodule
