// Logisim project 2-23.circ as structural Verilog
module _2_23_a (
  input  A,
  input  B,
  input  C,
  output F
);

  wire and_1_out, and_2_out, and_3_out, not_1_out, not_2_out, not_3_out;

  not not_1 (not_1_out, A);
  not not_2 (not_2_out, B);
  not not_3 (not_3_out, C);
  and and_1 (and_1_out, not_1_out, B);
  and and_2 (and_2_out, not_2_out, C);
  and and_3 (and_3_out, not_1_out, not_2_out, C);
  or or_1 (F, and_1_out, and_2_out, and_3_out);

  // Notes on the sheet:
  //   F = A'B + A'B'C + B'C
endmodule

module _2_23_b (
  input  w,
  input  x,
  input  y,
  input  z,
  output F
);

  wire not_1_out, not_2_out, not_3_out, not_4_out, or_1_out, or_2_out, or_3_out;

  not not_1 (not_1_out, w);
  not not_2 (not_2_out, x);
  not not_3 (not_3_out, y);
  not not_4 (not_4_out, z);
  or or_1 (or_1_out, not_1_out, x);
  or or_2 (or_2_out, x, y);
  or or_3 (or_3_out, w, not_4_out);
  and and_1 (F, or_1_out, or_2_out, or_3_out);

  // Notes on the sheet:
  //   F = (w' + x)(x + y)(w + z')
endmodule

module _2_23_c (
  input  A,
  input  B,
  input  C,
  input  D,
  output F
);

  wire and_1_out, and_2_out, not_1_out, not_2_out, not_3_out, not_4_out, or_1_out, or_2_out;

  not not_1 (not_1_out, A);
  not not_2 (not_2_out, B);
  not not_3 (not_3_out, C);
  not not_4 (not_4_out, D);
  or or_1 (or_1_out, A, B);
  and and_1 (and_1_out, or_1_out, or_2_out);
  or or_2 (or_2_out, not_2_out, not_3_out);
  and and_2 (and_2_out, A, D);
  or or_3 (F, and_1_out, and_2_out);

  // Notes on the sheet:
  //   F = (A + B)(B' + C') + AD
endmodule

module _2_24_d (
  input  w,
  input  x,
  input  y,
  input  z,
  output out_5
);

  wire and_1_out, and_2_out, and_3_out, not_1_out, not_2_out, not_3_out, not_4_out, or_1_out;

  not not_1 (not_1_out, w);
  not not_2 (not_2_out, x);
  not not_3 (not_3_out, y);
  not not_4 (not_4_out, z);
  and and_1 (and_1_out, not_1_out, not_2_out, not_3_out);
  and and_2 (and_2_out, w, x);
  and and_3 (and_3_out, and_2_out, or_1_out);
  or or_1 (or_1_out, y, z);
  or or_2 (out_5, and_1_out, and_3_out);

  // Notes on the sheet:
  //   F = w'x'y' + wx(y + z)
endmodule
