// Logisim project 2-27.circ as structural Verilog
module f1 (
  input  a,
  input  b,
  input  c,
  output f1
);

  wire and_1_out, and_2_out, and_3_out, not_1_out, not_2_out, not_3_out;

  not not_1 (not_1_out, a);
  not not_2 (not_2_out, b);
  not not_3 (not_3_out, c);
  and and_1 (and_1_out, not_1_out, not_2_out, not_3_out);
  and and_2 (and_2_out, a, b);
  and and_3 (and_3_out, b, c);
  or or_1 (f1, and_1_out, and_2_out, and_3_out);

  // Notes on the sheet:
  //   f1 = a'b'c' + ab + bc
endmodule

module f2 (
  input  a,
  input  b,
  input  c,
  output f2
);

  wire and_1_out, and_2_out, and_3_out, not_1_out, not_2_out, not_3_out;

  not not_1 (not_1_out, a);
  not not_2 (not_2_out, b);
  not not_3 (not_3_out, c);
  and and_1 (and_1_out, not_1_out, b);
  and and_2 (and_2_out, b, not_3_out);
  and and_3 (and_3_out, a, not_2_out);
  or or_1 (f2, and_1_out, and_2_out, and_3_out);

  // Notes on the sheet:
  //   f2 = a'b + bc' + ab'
endmodule
