// Logisim project 2-28.circ as structural Verilog
module _2_28_a (
  input  a,
  input  b,
  input  c,
  output out_4
);

  wire nor_1_out, nor_2_out, not_1_out, not_2_out, not_3_out;

  not not_1 (not_1_out, a);
  not not_2 (not_2_out, b);
  not not_3 (not_3_out, c);
  nor nor_1 (nor_1_out, a, b);
  nor nor_2 (nor_2_out, b, not_3_out);
  nand nand_1 (out_4, nor_1_out, nor_2_out);

  // Notes on the sheet:
  //   y = a + b + c'
endmodule
