// Logisim project 2-5.circ as structural Verilog
module _2_2_a (
  input  x,
  input  y,
  input  x_2,
  input  y_2,
  output F,
  output F_2
);

  wire and_1_out, and_2_out, and_3_out, not_1_out, not_2_out;

  not not_1 (not_1_out, x);
  not not_2 (not_2_out, y);
  or or_1 (F_2, x_2, y_2);
  and and_1 (and_1_out, x, y);
  and and_2 (and_2_out, x, not_2_out);
  and and_3 (and_3_out, not_1_out, y);
  or or_2 (F, and_1_out, and_2_out, and_3_out);

  // Notes on the sheet:
  //   F = xy + xy' + x'y
  //   F = x + y
endmodule

module _2_2_b (
  input  x,
  input  y,
  input  y_2,
  output F,
  output F_2
);

  wire not_1_out, not_2_out, or_1_out, or_2_out;

  not not_1 (not_1_out, x);
  not not_2 (not_2_out, y);
  or or_1 (or_1_out, x, y);
  or or_2 (or_2_out, not_1_out, y);
  and and_1 (F, or_1_out, or_2_out);

  assign F_2 = y_2;

  // Notes on the sheet:
  //   F = (x+y)(x'+y)
  //   F = y
endmodule

module _2_2_c (
  input  x,
  input  y,
  input  x_2,
  input  y_2,
  output F,
  output F_2
);

  wire and_2_out, not_1_out, not_2_out, not_3_out, or_1_out;

  not not_1 (not_1_out, x);
  not not_2 (not_2_out, y);
  and and_1 (F_2, x_2, y_2);
  not not_3 (not_3_out, or_1_out);
  or or_1 (or_1_out, not_1_out, not_2_out);
  and and_2 (and_2_out, x, y);
  and and_3 (F, not_3_out, and_2_out);

  // Notes on the sheet:
  //   F = xy
  //   F = xy(x'+y')'
endmodule
