// Logisim project 2-6.circ as structural Verilog
module _2_3_a (
  input  x,
  input  y,
  input  z,
  input  y_2,
  output F,
  output F_2
);

  wire and_1_out, and_2_out, and_3_out, not_1_out, not_2_out, not_3_out;

  not not_1 (not_1_out, x);
  not not_2 (not_2_out, y);
  not not_3 (not_3_out, z);
  and and_1 (and_1_out, x, y, z);
  and and_2 (and_2_out, not_1_out, y);
  and and_3 (and_3_out, x, y, not_3_out);
  or or_1 (F, and_1_out, and_2_out, and_3_out);

  assign F_2 = y_2;

  // Notes on the sheet:
  //   F = y
  //   F = xyz + x'y + xyz'
endmodule

module _2_3_c (
  input  x,
  input  y,
  input  x_2,
  input  y_2,
  output F,
  output F_2
);

  wire not_1_out, not_2_out, not_3_out, not_4_out, not_5_out, or_1_out, or_2_out;

  not not_1 (not_1_out, x);
  not not_2 (not_2_out, x_2);
  not not_3 (not_3_out, y);
  not not_4 (not_4_out, y_2);
  or or_1 (or_1_out, x, y);
  or or_2 (or_2_out, not_1_out, not_3_out);
  and and_1 (F_2, not_2_out, not_4_out);
  not not_5 (not_5_out, or_1_out);
  and and_2 (F, not_5_out, or_2_out);

  // Notes on the sheet:
  //   F = x'y'
  //   F = (x + y)'(x' + y')
endmodule

module _2_3_f (
  input  x,
  input  y,
  input  z,
  input  x_2,
  input  y_2,
  input  z_2,
  output F,
  output out_8
);

  wire and_1_out, not_1_out, not_2_out, not_3_out, not_4_out, not_5_out, not_6_out, or_1_out, or_2_out;

  not not_1 (not_1_out, x);
  not not_2 (not_2_out, x_2);
  not not_3 (not_3_out, y);
  not not_4 (not_4_out, y_2);
  not not_5 (not_5_out, z);
  not not_6 (not_6_out, z_2);
  or or_1 (or_1_out, not_1_out, not_5_out);
  or or_2 (or_2_out, x, not_3_out, not_5_out);
  and and_1 (and_1_out, not_2_out, not_4_out);
  and and_2 (F, or_1_out, or_2_out);
  or or_3 (out_8, and_1_out, not_6_out);

  // Notes on the sheet:
  //   F = x'y' + z'
  //   F = (x' + z')(x + y' + z')
endmodule
