// Logisim project 2-7.circ as structural Verilog
module _2_4_b (
  input  x,
  input  y,
  input  z,
  input  w,
  input  x_2,
  input  y_2,
  input  z_2,
  input  w_2,
  output F,
  output F_2
);

  wire and_1_out, and_2_out, and_3_out, not_1_out, not_2_out, not_3_out, not_4_out, not_5_out, not_6_out,
       not_7_out, not_8_out, or_1_out, or_2_out, or_3_out;

  not not_1 (not_1_out, x);
  not not_2 (not_2_out, x_2);
  not not_3 (not_3_out, y);
  not not_4 (not_4_out, y_2);
  not not_5 (not_5_out, z);
  not not_6 (not_6_out, z_2);
  not not_7 (not_7_out, w);
  not not_8 (not_8_out, w_2);
  and and_1 (and_1_out, y, z);
  and and_2 (and_2_out, not_8_out, x_2);
  and and_3 (and_3_out, not_8_out, y_2, z_2);
  or or_1 (or_1_out, not_7_out, y);
  or or_2 (or_2_out, not_7_out, not_3_out);
  or or_3 (or_3_out, w, x, and_1_out);
  or or_4 (F_2, and_2_out, and_3_out);
  and and_4 (F, or_1_out, or_2_out, or_3_out);

  // Notes on the sheet:
  //   F = w'x + w'yz
  //   F = (w' + y)(w' + y')(w + x + yz)
endmodule

module _2_4_a (
  input  x,
  input  y,
  input  z,
  input  x_2,
  input  y_2,
  input  z_2,
  output F,
  output F_2
);

  wire and_1_out, and_2_out, and_3_out, and_4_out, and_5_out, not_1_out, not_2_out, not_3_out, not_4_out,
       not_5_out, not_6_out;

  not not_1 (not_1_out, x);
  not not_2 (not_2_out, x_2);
  not not_3 (not_3_out, y);
  not not_4 (not_4_out, y_2);
  not not_5 (not_5_out, z);
  not not_6 (not_6_out, z_2);
  and and_1 (and_1_out, not_1_out, not_3_out, z);
  and and_2 (and_2_out, not_1_out, y, z);
  and and_3 (and_3_out, x, not_3_out);
  and and_4 (and_4_out, not_2_out, z_2);
  and and_5 (and_5_out, x_2, not_4_out);
  or or_1 (F, and_1_out, and_2_out, and_3_out);
  or or_2 (F_2, and_4_out, and_5_out);

  // Notes on the sheet:
  //   F = x'y'z + x'yz + xy'
  //   F = x'z + xy'
endmodule
