// Logisim project 3-16.circ as structural Verilog
module _3_16_d (
  input  A,
  input  B,
  input  C,
  input  D,
  output out_5
);

  wire nand_1_out, nand_2_out, not_1_out, not_2_out, not_3_out, not_4_out;

  not not_1 (not_1_out, A);
  not not_2 (not_2_out, B);
  not not_3 (not_3_out, C);
  not not_4 (not_4_out, D);
  nand nand_1 (nand_1_out, B, D);
  nand nand_2 (nand_2_out, A, D);
  nand nand_3 (out_5, nand_1_out, nand_2_out);

  // Notes on the sheet:
  //   F = BD + AD
endmodule

module _3_16_b (
  input  A,
  input  B,
  input  C,
  input  D,
  output Y
);

  wire nand_1_out, nand_2_out, nand_3_out, not_1_out, not_2_out, not_3_out, not_4_out;

  not not_1 (not_1_out, A);
  not not_2 (not_2_out, B);
  not not_3 (not_3_out, C);
  not not_4 (not_4_out, D);
  nand nand_1 (nand_1_out, B, D);
  nand nand_2 (nand_2_out, not_1_out, C, not_4_out);
  nand nand_3 (nand_3_out, A, C, not_4_out);
  nand nand_4 (Y, nand_1_out, nand_2_out, nand_3_out);

  // Notes on the sheet:
  //   F = BD + A'CD' + ACD
endmodule

module _3_16_c (
  input  A,
  input  B,
  input  C,
  input  D,
  output F
);

  wire nand_1_out, nand_2_out, not_1_out, not_2_out, not_3_out, not_4_out;

  not not_1 (not_1_out, A);
  not not_2 (not_2_out, B);
  not not_3 (not_3_out, C);
  not not_4 (not_4_out, D);
  nand nand_1 (nand_1_out, not_1_out, not_3_out);
  nand nand_2 (nand_2_out, not_1_out, D);
  nand nand_3 (F, nand_1_out, nand_2_out, not_2_out);

  // Notes on the sheet:
  //   F = B' + A'C' + A'D
endmodule

module _3_16_a (
  input  A,
  input  B,
  input  C,
  input  D,
  output F
);

  wire nand_1_out, nand_2_out, not_1_out, not_2_out, not_3_out, not_4_out;

  not not_1 (not_1_out, A);
  not not_2 (not_2_out, B);
  not not_3 (not_3_out, C);
  not not_4 (not_4_out, D);
  nand nand_1 (nand_1_out, not_1_out, C);
  nand nand_2 (nand_2_out, B, C);
  nand nand_3 (F, nand_1_out, nand_2_out);

  // Notes on the sheet:
  //   F = A'C + BC
endmodule
