// Logisim project 3-17.circ as structural Verilog
module _3_17_B (
  input  A,
  input  B,
  input  C,
  input  D,
  output out_5
);

  wire nor_1_out, nor_2_out, nor_3_out, nor_4_out, not_1_out, not_2_out, not_3_out, not_4_out;

  not not_1 (not_1_out, A);
  not not_2 (not_2_out, B);
  not not_3 (not_3_out, C);
  not not_4 (not_4_out, D);
  nor nor_1 (nor_1_out, A, B);
  nor nor_2 (nor_2_out, C, D);
  nor nor_3 (nor_3_out, B, C);
  nor nor_4 (nor_4_out, nor_1_out, nor_2_out, nor_3_out);
  nor nor_5 (out_5, nor_4_out, nor_4_out);

  // Notes on the sheet:
  //   F = A'B' + C'D' + B'C'
endmodule

module _3_17_A (
  input  A,
  input  B,
  input  C,
  input  D,
  output F
);

  wire nand_1_out, nand_2_out, nand_3_out, not_1_out, not_2_out, not_3_out, not_4_out;

  not not_1 (not_1_out, A);
  not not_2 (not_2_out, B);
  not not_3 (not_3_out, C);
  not not_4 (not_4_out, D);
  nand nand_1 (nand_1_out, not_1_out, not_2_out);
  nand nand_2 (nand_2_out, not_3_out, not_4_out);
  nand nand_3 (nand_3_out, not_2_out, not_3_out);
  nand nand_4 (F, nand_1_out, nand_2_out, nand_3_out);

  // Notes on the sheet:
  //   F = A'B' + C'D' + B'C'
endmodule
