// Logisim project 3-18.circ as structural Verilog: 1 circuit, main circuit main
module main (
  input  A,
  input  B,
  input  C,
  input  D,
  output out_5,
  output out_6,
  output out_7,
  output out_8
);

  wire and_1_out, and_2_out, and_3_out, and_4_out, nand_1_out, nand_2_out, nand_3_out, nand_4_out,
       nand_5_out, nand_6_out, nand_7_out, nor_1_out, nor_2_out, nor_3_out, nor_4_out, nor_5_out, nor_6_out,
       not_1_out, not_2_out, not_3_out, not_4_out, or_1_out, or_2_out, xnor_1_out, xor_1_out;

  not not_1 (not_1_out, A);
  not not_2 (not_2_out, B);
  not not_3 (not_3_out, C);
  not not_4 (not_4_out, D);
  xnor xnor_1 (xnor_1_out, A, B);
  xor xor_1 (xor_1_out, C, D);
  and and_1 (and_1_out, not_1_out, not_2_out);
  and and_2 (and_2_out, A, B);
  and and_3 (and_3_out, not_3_out, D);
  and and_4 (and_4_out, C, not_4_out);
  nor nor_1 (nor_1_out, A, B);
  nor nor_2 (nor_2_out, not_1_out, not_2_out);
  nor nor_3 (nor_3_out, C, not_4_out);
  nor nor_4 (nor_4_out, not_3_out, D);
  nand nand_1 (nand_1_out, not_1_out, not_2_out);
  nand nand_2 (nand_2_out, A, B);
  nand nand_3 (nand_3_out, not_3_out, D);
  nand nand_4 (nand_4_out, C, not_4_out);
  or or_1 (or_1_out, and_1_out, and_2_out);
  or or_2 (or_2_out, and_3_out, and_4_out);
  nor nor_5 (nor_5_out, nor_1_out, nor_2_out);
  nor nor_6 (nor_6_out, nor_3_out, nor_4_out);
  nand nand_5 (nand_5_out, nand_1_out, nand_2_out);
  nand nand_6 (nand_6_out, nand_3_out, nand_4_out);
  and and_5 (out_5, xnor_1_out, xor_1_out);
  and and_6 (out_6, or_1_out, or_2_out);
  nor nor_7 (out_7, nor_5_out, nor_6_out);
  nand nand_7 (nand_7_out, nand_5_out, nand_6_out);
  nand nand_8 (out_8, nand_7_out, nand_7_out);

  // Notes on the sheet:
  //   AND-OR Implementation
  //   NOR Implementation
  //   NAND Implementation
endmodule
