// Logisim project 3-19.circ as structural Verilog
module _3_19_a (
  input  w,
  input  x,
  input  y,
  input  z,
  output out_5,
  output out_6
);

  wire and_1_out, and_2_out, and_3_out, nor_1_out, nor_2_out, nor_3_out, nor_5_out, not_1_out, not_2_out,
       not_3_out, not_4_out;

  not not_1 (not_1_out, w);
  not not_2 (not_2_out, x);
  not not_3 (not_3_out, y);
  not not_4 (not_4_out, z);
  and and_1 (and_1_out, w, not_2_out);
  and and_2 (and_2_out, not_3_out, not_4_out);
  and and_3 (and_3_out, w, not_4_out);
  nor nor_1 (nor_1_out, not_1_out, x);
  nor nor_2 (nor_2_out, y, z);
  nor nor_3 (nor_3_out, not_1_out, z);
  or or_1 (out_5, and_1_out, and_2_out, and_3_out);
  nor nor_4 (out_6, nor_5_out, nor_5_out);
  nor nor_5 (nor_5_out, nor_1_out, nor_2_out, nor_3_out);

  // Notes on the sheet:
  //   F = wx' + y'z' + wz' 
endmodule

module _3_19_b (
  input  w,
  input  x,
  input  y,
  input  z,
  output out_5
);

  wire nor_1_out, nor_2_out, nor_3_out, nor_4_out, nor_5_out, nor_6_out, not_1_out, not_2_out, not_3_out,
       not_4_out;

  not not_1 (not_1_out, w);
  not not_2 (not_2_out, x);
  not not_3 (not_3_out, y);
  not not_4 (not_4_out, z);
  nor nor_1 (nor_1_out, w, x);
  nor nor_2 (nor_2_out, nor_1_out, nor_3_out);
  nor nor_3 (nor_3_out, not_1_out, not_2_out);
  nor nor_4 (nor_4_out, y, not_4_out);
  nor nor_5 (nor_5_out, nor_4_out, nor_6_out);
  nor nor_6 (nor_6_out, not_3_out, z);
  nor nor_7 (out_5, nor_2_out, nor_5_out);

  // Notes on the sheet:
  //   F = (w'x' + wx)(y'z + yz')
endmodule

module _3_19_c (
  input  x,
  input  y,
  input  z,
  output out_4,
  output out_5
);

  wire and_1_out, and_2_out, nor_1_out, nor_2_out, nor_3_out, not_1_out, not_2_out, not_3_out;

  not not_1 (not_1_out, x);
  not not_2 (not_2_out, y);
  not not_3 (not_3_out, z);
  and and_1 (and_1_out, not_1_out, not_2_out);
  and and_2 (and_2_out, x, not_3_out);
  nor nor_1 (nor_1_out, x, y);
  nor nor_2 (nor_2_out, not_1_out, z);
  or or_1 (out_4, and_1_out, and_2_out);
  nor nor_3 (nor_3_out, nor_1_out, nor_2_out);
  nor nor_4 (out_5, nor_3_out, nor_3_out);

  // Notes on the sheet:
  //   F = x'y' + xz'
endmodule
