// Logisim project 3-20.circ as structural Verilog: 1 circuit, main circuit main
module main (
  input  A,
  input  B,
  input  C,
  input  D,
  input  E,
  output F,
  output F_2,
  output F_3
);

  wire and_1_out, and_2_out, and_3_out, and_4_out, and_5_out, nand_1_out, nand_2_out, nand_3_out, nand_4_out,
       nand_5_out, nand_6_out, nand_7_out, nand_8_out, nor_1_out, nor_2_out, nor_3_out, nor_4_out, nor_5_out,
       nor_6_out, nor_7_out, nor_8_out, nor_9_out, not_1_out, not_2_out, not_3_out, not_4_out, not_5_out,
       or_1_out, or_2_out;

  not not_1 (not_1_out, A);
  not not_2 (not_2_out, B);
  not not_3 (not_3_out, C);
  not not_4 (not_4_out, D);
  not not_5 (not_5_out, E);
  and and_1 (and_1_out, A, not_2_out);
  and and_2 (and_2_out, C, not_4_out);
  and and_3 (and_3_out, B, C);
  or or_1 (or_1_out, A, B);
  nor nor_1 (nor_1_out, not_1_out, B);
  nor nor_2 (nor_2_out, not_3_out, D);
  nor nor_3 (nor_3_out, not_2_out, not_3_out);
  nor nor_4 (nor_4_out, A, B);
  nand nand_1 (nand_1_out, A, not_2_out);
  nand nand_2 (nand_2_out, C, not_4_out);
  nand nand_3 (nand_3_out, B, C);
  nand nand_4 (nand_4_out, not_1_out, not_2_out);
  or or_2 (or_2_out, and_1_out, and_2_out);
  nor nor_5 (nor_5_out, nor_1_out, nor_2_out);
  nor nor_6 (nor_6_out, nor_3_out, nor_3_out);
  nand nand_5 (nand_5_out, nand_1_out, nand_2_out);
  nand nand_6 (nand_6_out, nand_3_out, nand_3_out);
  and and_4 (and_4_out, or_2_out, E);
  and and_5 (and_5_out, and_3_out, or_1_out);
  nor nor_7 (nor_7_out, nor_5_out, not_5_out);
  nor nor_8 (nor_8_out, nor_6_out, nor_4_out);
  nand nand_7 (nand_7_out, nand_5_out, E);
  nand nand_8 (nand_8_out, nand_6_out, nand_4_out);
  or or_3 (F, and_4_out, and_5_out);
  nor nor_9 (nor_9_out, nor_7_out, nor_8_out);
  nand nand_9 (F_3, nand_7_out, nand_8_out);
  nor nor_10 (F_2, nor_9_out, nor_9_out);

  // Notes on the sheet:
  //   F = (AB' + CD')E + BC(A + B)
  //   NOR Implementation
  //   NAND Implementation
endmodule
