// Logisim project 3-21.circ as structural Verilog: 1 circuit, main circuit main
module main (
  input  w,
  input  x,
  input  y,
  input  z,
  output out_5,
  output out_6,
  output out_7
);

  wire and_1_out, and_2_out, nand_1_out, nand_2_out, nand_3_out, nor_1_out, nor_2_out, nor_3_out, nor_5_out,
       not_1_out, not_2_out, not_3_out, not_4_out, or_1_out;

  not not_1 (not_1_out, w);
  not not_2 (not_2_out, x);
  not not_3 (not_3_out, y);
  not not_4 (not_4_out, z);
  or or_1 (or_1_out, x, y, z);
  and and_1 (and_1_out, x, y, z);
  nand nand_1 (nand_1_out, not_2_out, not_3_out, not_4_out);
  nand nand_2 (nand_2_out, x, y, z);
  nor nor_1 (nor_1_out, x, y, z);
  nor nor_2 (nor_2_out, not_2_out, not_3_out, not_4_out);
  and and_2 (and_2_out, or_1_out, w);
  nand nand_3 (nand_3_out, nand_1_out, w);
  or or_2 (out_5, and_2_out, and_1_out);
  nand nand_4 (out_6, nand_3_out, nand_2_out);
  nor nor_3 (nor_3_out, nor_1_out, not_1_out);
  nor nor_4 (out_7, nor_5_out, nor_5_out);
  nor nor_5 (nor_5_out, nor_3_out, nor_2_out);

  // Notes on the sheet:
  //   F = w(x + y +z) + xyz
  //   NAND Implementation
  //   NOR Implementation
endmodule
