// Logisim project 3-22.circ as structural Verilog: 1 circuit, main circuit main
module main (
  input  A,
  input  B,
  input  C,
  input  D,
  output z,
  output y,
  output x,
  output w,
  output z_2,
  output y_2,
  output x_2,
  output w_2
);

  wire and_1_out, and_2_out, and_3_out, and_4_out, nand_1_out, nand_2_out, nand_3_out, nand_5_out,
       nand_6_out, nand_7_out, not_1_out, not_2_out, not_3_out, not_5_out, or_1_out;

  not not_1 (not_1_out, A);
  not not_2 (not_2_out, B);
  not not_3 (not_3_out, C);
  not not_4 (z, D);
  and and_1 (and_1_out, C, D);
  or or_1 (or_1_out, C, D);
  nand nand_1 (nand_1_out, C, D);
  nand nand_2 (nand_2_out, not_3_out, z);
  not not_5 (not_5_out, or_1_out);
  nand nand_3 (nand_3_out, nand_2_out, nand_2_out);
  or or_2 (y, and_1_out, not_5_out);
  and and_2 (and_2_out, not_5_out, B);
  and and_3 (and_3_out, or_1_out, not_2_out);
  and and_4 (and_4_out, or_1_out, B);
  nand nand_4 (y_2, nand_1_out, nand_2_out);
  nand nand_5 (nand_5_out, nand_3_out, B);
  nand nand_6 (nand_6_out, nand_2_out, not_2_out);
  nand nand_7 (nand_7_out, nand_2_out, B);
  or or_3 (x, and_2_out, and_3_out);
  or or_4 (w, and_4_out, A);
  nand nand_8 (x_2, nand_5_out, nand_6_out);
  nand nand_9 (w_2, nand_7_out, not_1_out);

  assign z_2 = z;

  // Notes on the sheet:
  //   NAND Implementation
endmodule
