// Logisim project 3-23.circ as structural Verilog: 1 circuit, main circuit main
module main (
  input  A,
  input  B,
  input  C,
  input  D,
  output out_5,
  output out_6
);

  wire nor_1_out, not_1_out, not_2_out, not_3_out, not_4_out, or_1_out;

  not not_1 (not_1_out, A);
  not not_2 (not_2_out, B);
  not not_3 (not_3_out, C);
  not not_4 (not_4_out, D);
  or or_1 (or_1_out, not_1_out, not_2_out, not_3_out);
  nor nor_1 (nor_1_out, not_1_out, not_2_out, not_3_out);
  and and_1 (out_5, or_1_out, not_4_out);
  nor nor_2 (out_6, nor_1_out, D);

  // Notes on the sheet:
  //   F = (C' + B' + A')D'
  //   NOR Implementation
endmodule
