// Logisim project 3-24.circ as structural Verilog: 1 circuit, main circuit main
module main (
  input  A,
  input  B,
  input  C,
  input  D,
  output out_5,
  output out_6,
  output out_7,
  output out_8,
  output out_9
);

  wire and_1_out, and_2_out, and_3_out, and_4_out, and_5_out, and_6_out, nand_1_out, nand_2_out, nand_3_out,
       nor_1_out, nor_2_out, nor_3_out, not_1_out, not_2_out, not_3_out, not_4_out, or_1_out, or_2_out,
       or_3_out;

  not not_1 (not_1_out, A);
  not not_2 (not_2_out, B);
  not not_3 (not_3_out, C);
  not not_4 (not_4_out, D);
  and and_1 (and_1_out, not_3_out, not_4_out);
  and and_2 (and_2_out, A, not_2_out);
  and and_3 (and_3_out, A, not_4_out);
  nand nand_1 (nand_1_out, B, D);
  nand nand_2 (nand_2_out, not_1_out, C);
  nand nand_3 (nand_3_out, not_1_out, D);
  and and_4 (and_4_out, B, D);
  and and_5 (and_5_out, not_1_out, C);
  and and_6 (and_6_out, not_1_out, D);
  nor nor_1 (nor_1_out, C, D);
  nor nor_2 (nor_2_out, not_1_out, B);
  nor nor_3 (nor_3_out, not_1_out, D);
  or or_1 (or_1_out, C, D);
  or or_2 (or_2_out, not_1_out, B);
  or or_3 (or_3_out, not_1_out, D);
  or or_4 (out_5, and_1_out, and_2_out, and_3_out);
  and and_7 (out_6, nand_1_out, nand_2_out, nand_3_out);
  nor nor_4 (out_7, and_4_out, and_5_out, and_6_out);
  or or_5 (out_8, nor_1_out, nor_2_out, nor_3_out);
  nand nand_4 (out_9, or_1_out, or_2_out, or_3_out);

  // Notes on the sheet:
  //   F = C'D' + AB' + AD'
  //   F = (B' + D')(A + C')(A + D')
  //   NAND-AND
  //   AND-NOR
  //   NOR-OR
  //   OR-NAND
endmodule
