// Logisim project 3-28.circ as structural Verilog
module _3_bit_odd_parity (
  input  x,
  input  y,
  input  z,
  output out_4
);

  wire and_1_out, and_2_out, and_3_out, and_4_out, not_1_out, not_2_out, not_3_out;

  not not_1 (not_1_out, x);
  not not_2 (not_2_out, y);
  not not_3 (not_3_out, z);
  and and_1 (and_1_out, not_1_out, not_2_out, not_3_out);
  and and_2 (and_2_out, x, not_2_out, z);
  and and_3 (and_3_out, not_1_out, y, z);
  and and_4 (and_4_out, x, y, not_3_out);
  or or_1 (out_4, and_1_out, and_2_out, and_3_out, and_4_out);

  // Notes on the sheet:
  //   F = ((x XOR y) XOR z)'
endmodule

module _4_bit_parity_checker (
  input  x,
  input  y,
  input  z,
  input  P,
  output out_5
);

  wire not_1_out, not_2_out, not_3_out, not_4_out, xor_1_out, xor_2_out;

  not not_1 (not_1_out, x);
  not not_2 (not_2_out, y);
  not not_3 (not_3_out, z);
  not not_4 (not_4_out, P);
  xor xor_1 (xor_1_out, x, y);
  xor xor_2 (xor_2_out, z, P);
  xnor xnor_1 (out_5, xor_1_out, xor_2_out);

  // Notes on the sheet:
  //   F = (x XOR y) NOR (z XOR P)
endmodule
