// Logisim project 3-29.circ as structural Verilog: 6 circuits, main circuit main
module main (
  input  A,
  input  B,
  input  C,
  output D,
  output E,
  output F,
  output G
);

  wire half_adder_1_c, half_adder_1_s, not_1_out, not_2_out, not_3_out;

  not not_1 (not_1_out, A);
  not not_2 (not_2_out, B);
  not not_3 (not_3_out, C);
  half_adder half_adder_1 (.S(half_adder_1_s), .C(half_adder_1_c), .a(B), .b(A));
  half_adder half_adder_2 (.S(D), .C(E), .a(C), .b(half_adder_1_s));
  half_adder half_adder_3 (.S(F), .C(G), .a(C), .b(half_adder_1_c));
endmodule

module half_adder (
  input  a,
  input  b,
  output S,
  output C
);

  xor xor_1 (S, a, b);
  and and_1 (C, a, b);
endmodule

module D (
  input  A,
  input  B,
  input  C,
  output out_4,
  output out_5
);

  wire half_adder_1_s, not_1_out, not_2_out, not_3_out, xor_1_out;

  not not_1 (not_1_out, A);
  not not_2 (not_2_out, B);
  not not_3 (not_3_out, C);
  half_adder half_adder_1 (.S(half_adder_1_s), .a(B), .b(A));  // open: C
  xor xor_1 (xor_1_out, A, B);
  half_adder half_adder_2 (.S(out_5), .a(C), .b(half_adder_1_s));  // open: C
  xor xor_2 (out_4, xor_1_out, C);
endmodule

module E (
  input  A,
  input  B,
  input  C,
  output out_4,
  output out_5
);

  wire and_1_out, and_2_out, half_adder_1_s, not_1_out, not_2_out, not_3_out;

  not not_1 (not_1_out, A);
  not not_2 (not_2_out, B);
  not not_3 (not_3_out, C);
  and and_1 (and_1_out, not_1_out, B, C);
  and and_2 (and_2_out, A, not_2_out, C);
  half_adder half_adder_1 (.S(half_adder_1_s), .a(B), .b(A));  // open: C
  or or_1 (out_4, and_1_out, and_2_out);
  half_adder half_adder_2 (.C(out_5), .a(C), .b(half_adder_1_s));  // open: S
endmodule

module F (
  input  A,
  input  B,
  input  C,
  output out_4,
  output out_5
);

  wire and_1_out, and_2_out, half_adder_1_c, not_1_out, not_2_out, not_3_out, or_1_out;

  not not_1 (not_1_out, A);
  not not_2 (not_2_out, B);
  not not_3 (not_3_out, C);
  and and_1 (and_1_out, A, B, not_3_out);
  or or_1 (or_1_out, not_1_out, not_2_out);
  half_adder half_adder_1 (.C(half_adder_1_c), .a(B), .b(A));  // open: S
  and and_2 (and_2_out, or_1_out, C);
  half_adder half_adder_2 (.S(out_5), .a(C), .b(half_adder_1_c));  // open: C
  or or_2 (out_4, and_1_out, and_2_out);
endmodule

module G (
  input  A,
  input  B,
  input  C,
  output out_4,
  output out_5
);

  wire half_adder_1_c, not_1_out, not_2_out, not_3_out;

  not not_1 (not_1_out, A);
  not not_2 (not_2_out, B);
  not not_3 (not_3_out, C);
  and and_1 (out_4, A, B, C);
  half_adder half_adder_1 (.C(half_adder_1_c), .a(B), .b(A));  // open: S
  half_adder half_adder_2 (.C(out_5), .a(C), .b(half_adder_1_c));  // open: S
endmodule
