// Logisim project 3-36.circ as structural Verilog
module _3_36_a (
  input  A,
  input  B,
  input  C,
  output F
);

  wire and_1_out, and_2_out, not_1_out, not_2_out, not_3_out, xor_1_out;

  not not_1 (not_1_out, A);
  not not_2 (not_2_out, B);
  not not_3 (not_3_out, C);
  xor xor_1 (xor_1_out, A, B);
  and and_1 (and_1_out, xor_1_out, C);
  and and_2 (and_2_out, A, B);
  or or_1 (F, and_1_out, and_2_out);
endmodule

module _3_36_b (
  input  A0,
  input  A1,
  input  B0,
  input  B1,
  output F3,
  output F2,
  output out_7
);

  wire and_2_out, and_3_out, not_1_out, not_2_out, not_3_out, not_4_out, or_1_out, xnor_1_out, xor_1_out;

  not not_1 (not_1_out, A0);
  not not_2 (not_2_out, A1);
  not not_3 (not_3_out, B0);
  not not_4 (not_4_out, B1);
  xor xor_1 (xor_1_out, A1, B1);
  xnor xnor_1 (xnor_1_out, A0, B0);
  and and_1 (F3, xnor_1_out, xor_1_out);
  and and_2 (and_2_out, B0, B1, not_1_out);
  or or_1 (or_1_out, B0, not_1_out, not_2_out);
  and and_3 (and_3_out, B1, not_2_out);
  or or_2 (F2, and_2_out, or_1_out, and_3_out);
  nor nor_1 (out_7, F3, F2);
endmodule

module _3_36_c (
  input  a,
  input  b,
  output y1,
  output y2
);

  wire not_1_out, not_2_out;

  not not_1 (not_1_out, a);
  not not_2 (not_2_out, b);
  and and_1 (y1, a, b);
  or or_1 (y2, a, b);
endmodule
