// Logisim project 4-20.circ as structural Verilog
module adder_4_bit (
  input  in_1,
  input  in_2,
  input  in_3,
  input  in_4,
  input  in_5,
  input  in_6,
  input  in_7,
  input  in_8,
  output out_9,
  output out_10,
  output out_11,
  output out_12,
  output out_13
);
endmodule

module multiplier_4_bit (
  input  A3,
  input  A2,
  input  A1,
  input  A0,
  input  B3,
  input  B2,
  input  B1,
  input  B0,
  output C7,
  output C6,
  output C5,
  output C4,
  output C3,
  output C2,
  output C1,
  output C0
);

  wire adder_4_bit_2_out_9, adder_4_bit_2_out_10, adder_4_bit_2_out_11, adder_4_bit_2_out_12,
       adder_4_bit_3_out_9, adder_4_bit_3_out_10, adder_4_bit_3_out_11, adder_4_bit_3_out_12, and_1_out,
       and_2_out, and_3_out, and_4_out, and_5_out, and_6_out, and_7_out, and_8_out, and_9_out, and_10_out,
       and_11_out, and_12_out, and_13_out, and_14_out, and_15_out;

  and and_1 (and_1_out, A3, B3);
  and and_2 (and_2_out, A3, B0);
  and and_3 (and_3_out, A3, B2);
  and and_4 (and_4_out, A3, B1);
  and and_5 (and_5_out, A2, B3);
  and and_6 (and_6_out, A2, B2);
  and and_7 (and_7_out, A2, B1);
  and and_8 (and_8_out, A2, B0);
  adder_4_bit adder_4_bit_1 (
    .in_1(adder_4_bit_2_out_12), .in_2(adder_4_bit_2_out_11), .in_3(adder_4_bit_2_out_10),
    .in_4(adder_4_bit_2_out_9), .in_5(and_2_out), .in_6(and_4_out), .in_7(and_3_out), .in_8(and_1_out),
    .out_9(C7), .out_10(C6), .out_11(C5), .out_12(C4), .out_13(C3));
  and and_9 (and_9_out, A1, B2);
  and and_10 (and_10_out, A1, B3);
  and and_11 (and_11_out, A1, B1);
  and and_12 (and_12_out, A1, B0);
  and and_13 (and_13_out, A0, B3);
  adder_4_bit adder_4_bit_2 (
    .in_1(adder_4_bit_3_out_12), .in_2(adder_4_bit_3_out_11), .in_3(adder_4_bit_3_out_10),
    .in_4(adder_4_bit_3_out_9), .in_5(and_8_out), .in_6(and_7_out), .in_7(and_6_out), .in_8(and_5_out),
    .out_9(adder_4_bit_2_out_9), .out_10(adder_4_bit_2_out_10), .out_11(adder_4_bit_2_out_11),
    .out_12(adder_4_bit_2_out_12), .out_13(C2));
  and and_14 (and_14_out, A0, B2);
  and and_15 (and_15_out, A0, B1);
  adder_4_bit adder_4_bit_3 (
    .in_1(and_15_out), .in_2(and_14_out), .in_3(and_13_out), .in_4(1'b0), .in_5(and_12_out),
    .in_6(and_11_out), .in_7(and_9_out), .in_8(and_10_out), .out_9(adder_4_bit_3_out_9),
    .out_10(adder_4_bit_3_out_10), .out_11(adder_4_bit_3_out_11), .out_12(adder_4_bit_3_out_12), .out_13(C1));
  and and_16 (C0, A0, B0);
endmodule
