// Logisim project 4-23.circ as structural Verilog: 1 circuit, main circuit main
module main (
  input  en,
  input  a,
  input  b,
  output out_4,
  output out_5,
  output out_6,
  output out_7,
  output out_8,
  output out_9,
  output out_10,
  output out_11,
  output out_12,
  output out_13,
  output out_14,
  output out_15
);

  wire nand_2_out, nand_4_out, nand_5_out, nand_7_out, not_1_out, not_2_out, not_3_out;

  not not_1 (not_1_out, en);
  not not_2 (not_2_out, a);
  not not_3 (not_3_out, b);
  and and_1 (out_4, not_2_out, not_3_out, en);
  and and_2 (out_5, not_2_out, b, en);
  and and_3 (out_6, a, not_3_out, en);
  and and_4 (out_7, a, b, en);
  nor nor_1 (out_8, a, b, not_1_out);
  nor nor_2 (out_9, a, not_3_out, not_1_out);
  nor nor_3 (out_10, not_2_out, b, not_1_out);
  nor nor_4 (out_11, not_2_out, not_3_out, not_1_out);
  nand nand_1 (out_12, nand_2_out, nand_2_out);
  nand nand_2 (nand_2_out, not_3_out, not_2_out, en);
  nand nand_3 (out_13, nand_4_out, nand_4_out);
  nand nand_4 (nand_4_out, not_2_out, b, en);
  nand nand_5 (nand_5_out, a, not_3_out, en);
  nand nand_6 (out_14, nand_5_out, nand_5_out);
  nand nand_7 (nand_7_out, a, b, en);
  nand nand_8 (out_15, nand_7_out, nand_7_out);

  // Notes on the sheet:
  //   4-23-a
  //   4-23-b
endmodule
