// Logisim project 4-25.circ as structural Verilog: 3 circuits, main circuit main
module main (
  input  [4:0] in_4_0,
  output [7:0] out_2,
  output [7:0] out_3,
  output [7:0] out_4,
  output [7:0] out_5
);

  wire [3:0] n2_to_4_decoder_1_out_3;

  _2_to_4_Decoder u_2_to_4_decoder_1 (.in_2(1'b1), .out_3(n2_to_4_decoder_1_out_3));  // open: in_1
  _3To8_Decoder u_3to8_decoder_1 (.in_1(in_4_0[2:0]), .in_2(n2_to_4_decoder_1_out_3[3]), .out_3(out_2));
  _3To8_Decoder u_3to8_decoder_2 (.in_1(in_4_0[2:0]), .in_2(n2_to_4_decoder_1_out_3[2]), .out_3(out_3));
  _3To8_Decoder u_3to8_decoder_3 (.in_1(in_4_0[2:0]), .in_2(n2_to_4_decoder_1_out_3[1]), .out_3(out_4));
  _3To8_Decoder u_3to8_decoder_4 (.in_1(in_4_0[2:0]), .in_2(n2_to_4_decoder_1_out_3[0]), .out_3(out_5));

  // Notes on the sheet:
  //   5X32 Decoder
  //   out[31:24]
  //   out[23:16]
  //   out[15:8]
  //   out[7:0]
endmodule

module _3To8_Decoder (
  input  [2:0] in_1,
  input  in_2,
  output [7:0] out_3
);
endmodule

module _2_to_4_Decoder (
  input  [1:0] in_1,
  input  in_2,
  output [3:0] out_3
);
endmodule
