// Logisim project 4-26.circ as structural Verilog: 2 circuits, main circuit main
module main (
  input  [3:0] in_3_0,
  output [3:0] out_15_12,
  output [3:0] out_11_8,
  output [3:0] out_7_4,
  output [3:0] out_3_0
);

  wire [3:0] n2_to_4_decoder_1_out_3;

  _2_to_4_Decoder u_2_to_4_decoder_1 (.in_1(in_3_0[3:2]), .in_2(1'b1), .out_3(n2_to_4_decoder_1_out_3));
  _2_to_4_Decoder u_2_to_4_decoder_2 (.in_1(in_3_0[1:0]), .in_2(n2_to_4_decoder_1_out_3[3]), .out_3(out_15_12));
  _2_to_4_Decoder u_2_to_4_decoder_3 (.in_1(in_3_0[1:0]), .in_2(n2_to_4_decoder_1_out_3[2]), .out_3(out_11_8));
  _2_to_4_Decoder u_2_to_4_decoder_4 (.in_1(in_3_0[1:0]), .in_2(n2_to_4_decoder_1_out_3[1]), .out_3(out_7_4));
  _2_to_4_Decoder u_2_to_4_decoder_5 (.in_1(in_3_0[1:0]), .in_2(n2_to_4_decoder_1_out_3[0]), .out_3(out_3_0));

  // Notes on the sheet:
  //   4X16 Decoder
endmodule

module _2_to_4_Decoder (
  input  [1:0] in_1,
  input  in_2,
  output [3:0] out_3
);
endmodule
