// Logisim project 4-27.circ as structural Verilog: 2 circuits, main circuit main
module main (
  input  [2:0] in_1,
  output F1,
  output F2,
  output F3
);

  wire [7:0] n3_to_8_decoder_1_out_3;

  _3_to_8_Decoder u_3_to_8_decoder_1 (.in_1(in_1), .in_2(1'b1), .out_3(n3_to_8_decoder_1_out_3));
  nand nand_1 (F1, n3_to_8_decoder_1_out_3[2], n3_to_8_decoder_1_out_3[5], n3_to_8_decoder_1_out_3[7]);
  nand nand_2 (F2, n3_to_8_decoder_1_out_3[0], n3_to_8_decoder_1_out_3[3]);
  nand nand_3 (F3, n3_to_8_decoder_1_out_3[0], n3_to_8_decoder_1_out_3[2], n3_to_8_decoder_1_out_3[3], n3_to_8_decoder_1_out_3[4], n3_to_8_decoder_1_out_3[7]);
endmodule

module _3_to_8_Decoder (
  input  [2:0] in_1,
  input  in_2,
  output [7:0] out_3
);
endmodule
