// Logisim project 4-31.circ as structural Verilog: 3 circuits, main circuit main
module main (
  input  [7:0] D7_D0,
  input  [7:0] D15_D8,
  input  S3,
  input  S2,
  input  S1,
  input  S0,
  output Y
);

  wire n8x1_mux_1_out_12, n8x1_mux_2_out_12;

  _8X1_MUX u_8x1_mux_1 (
    .in_1(S2), .in_2(S1), .in_3(S0), .in_4(D15_D8[7]), .in_5(D15_D8[6]), .in_6(D15_D8[5]), .in_7(D15_D8[4]),
    .in_8(D15_D8[3]), .in_9(D15_D8[2]), .in_10(D15_D8[1]), .in_11(D15_D8[0]), .out_12(n8x1_mux_1_out_12));
  _8X1_MUX u_8x1_mux_2 (
    .in_1(S2), .in_2(S1), .in_3(S0), .in_4(D7_D0[7]), .in_5(D7_D0[6]), .in_6(D7_D0[5]), .in_7(D7_D0[4]),
    .in_8(D7_D0[3]), .in_9(D7_D0[2]), .in_10(D7_D0[1]), .in_11(D7_D0[0]), .out_12(n8x1_mux_2_out_12));
  _2X1_MUL u_2x1_mul_1 (.in_1(S3), .in_2(n8x1_mux_1_out_12), .in_3(n8x1_mux_2_out_12), .out_4(Y));

  // Notes on the sheet:
  //   16X1 MUX
endmodule

module _8X1_MUX (
  input  in_1,
  input  in_2,
  input  in_3,
  input  in_4,
  input  in_5,
  input  in_6,
  input  in_7,
  input  in_8,
  input  in_9,
  input  in_10,
  input  in_11,
  output out_12
);
endmodule

module _2X1_MUL (
  input  in_1,
  input  in_2,
  input  in_3,
  output out_4
);
endmodule
