// Logisim project 4-32.circ as structural Verilog
module _8X1_MUX (
  input  in_1,
  input  in_2,
  input  in_3,
  input  in_4,
  input  in_5,
  input  in_6,
  input  in_7,
  input  in_8,
  input  in_9,
  input  in_10,
  input  in_11,
  output out_12
);
endmodule

module _2X1_MUL (
  input  in_1,
  input  in_2,
  input  in_3,
  output out_4
);
endmodule

module _4_32_a (
  input  A,
  input  B,
  input  C,
  input  D,
  output F
);

  wire not_1_out;

  not not_1 (not_1_out, D);
  _8X1_MUX u_8x1_mux_1 (
    .in_1(A), .in_2(B), .in_3(C), .in_4(not_1_out), .in_5(D), .in_6(1'b0), .in_7(1'b0), .in_8(D), .in_9(D),
    .in_10(D), .in_11(not_1_out), .out_12(F));
endmodule

module _4_32_b (
  input  A,
  input  B,
  input  C,
  input  D,
  output F
);

  wire not_1_out;

  not not_1 (not_1_out, D);
  _8X1_MUX u_8x1_mux_1 (
    .in_1(A), .in_2(B), .in_3(C), .in_4(1'b1), .in_5(D), .in_6(1'b1), .in_7(D), .in_8(1'b1), .in_9(1'b1),
    .in_10(not_1_out), .in_11(1'b1), .out_12(F));
endmodule
