// Logisim project 4-33.circ as structural Verilog: 4 circuits, main circuit main
module main (
  input  A,
  input  B,
  input  Cin,
  output S,
  output C
);

  wire not_1_out;

  not not_1 (not_1_out, Cin);
  _4X1_MUX u_4x1_mux_1 (.in_1(A), .in_2(B), .in_3(Cin), .in_4(not_1_out), .in_5(not_1_out), .in_6(Cin), .out_7(S));
  _4X1_MUX u_4x1_mux_2 (.in_1(A), .in_2(B), .in_3(1'b1), .in_4(Cin), .in_5(Cin), .in_6(1'b0), .out_7(C));

  // Notes on the sheet:
  //   FULL ADDER USING 4X1 MUX
endmodule

module _8X1_MUX (
  input  in_1,
  input  in_2,
  input  in_3,
  input  in_4,
  input  in_5,
  input  in_6,
  input  in_7,
  input  in_8,
  input  in_9,
  input  in_10,
  input  in_11,
  output out_12
);
endmodule

module _2X1_MUL (
  input  in_1,
  input  in_2,
  input  in_3,
  output out_4
);
endmodule

module _4X1_MUX (
  input  in_1,
  input  in_2,
  input  in_3,
  input  in_4,
  input  in_5,
  input  in_6,
  output out_7
);
endmodule
