// Logisim project 4-35.circ as structural Verilog: 6 circuits, main circuit main
module main (
  input  A,
  input  B,
  input  Cin,
  output S,
  output C
);

  wire not_1_out;

  not not_1 (not_1_out, Cin);
  _4X1_MUX u_4x1_mux_1 (.in_1(A), .in_2(B), .in_3(Cin), .in_4(not_1_out), .in_5(not_1_out), .in_6(Cin), .out_7(S));
  _4X1_MUX u_4x1_mux_2 (.in_1(A), .in_2(B), .in_3(1'b1), .in_4(Cin), .in_5(Cin), .in_6(1'b0), .out_7(C));

  // Notes on the sheet:
  //   FULL ADDER USING 4X1 MUX
endmodule

module _8X1_MUX (
  input  in_1,
  input  in_2,
  input  in_3,
  input  in_4,
  input  in_5,
  input  in_6,
  input  in_7,
  input  in_8,
  input  in_9,
  input  in_10,
  input  in_11,
  output out_12
);
endmodule

module _2X1_MUL (
  input  in_1,
  input  in_2,
  input  in_3,
  output out_4
);
endmodule

module _4X1_MUX (
  input  in_1,
  input  in_2,
  input  in_3,
  input  in_4,
  input  in_5,
  input  in_6,
  output out_7
);
endmodule

module _4_35_a (
  input  A,
  input  B,
  input  C,
  input  D,
  output S
);

  wire nor_1_out, not_1_out, xor_1_out;

  not not_1 (not_1_out, C);
  nor nor_1 (nor_1_out, C, D);
  xor xor_1 (xor_1_out, C, D);
  _4X1_MUX u_4x1_mux_1 (.in_1(A), .in_2(B), .in_3(xor_1_out), .in_4(nor_1_out), .in_5(D), .in_6(not_1_out), .out_7(S));
endmodule

module _4_35_b (
  input  A,
  input  B,
  input  C,
  input  D,
  output S
);

  wire not_1_out, xnor_1_out, xor_1_out;

  not not_1 (not_1_out, C);
  xor xor_1 (xor_1_out, C, D);
  xnor xnor_1 (xnor_1_out, C, D);
  _4X1_MUX u_4x1_mux_1 (.in_1(A), .in_2(B), .in_3(D), .in_4(1'b1), .in_5(xnor_1_out), .in_6(xor_1_out), .out_7(S));

  // Notes on the sheet:
  //   C
endmodule
