// Logisim project 5-1.circ as structural Verilog
module _5_a (
  input  D,
  input  En,
  output out_3,
  output out_4
);

  wire and_1_out, and_2_out, not_1_out;

  not not_1 (not_1_out, D);
  and and_1 (and_1_out, not_1_out, En);
  and and_2 (and_2_out, En, D);
  nor nor_1 (out_3, and_1_out, out_4);
  nor nor_2 (out_4, out_3, and_2_out);
endmodule

module _5_b (
  input  D,
  input  En,
  output out_3,
  output out_4
);

  wire nor_1_out, nor_2_out, not_1_out, not_2_out;

  not not_1 (not_1_out, En);
  not not_2 (not_2_out, D);
  nor nor_1 (nor_1_out, D, not_1_out);
  nor nor_2 (nor_2_out, not_1_out, not_2_out);
  nor nor_3 (out_3, nor_1_out, out_4);
  nor nor_4 (out_4, out_3, nor_2_out);
endmodule

module _5_c (
  input  D,
  input  En,
  output out_3,
  output out_4
);

  wire nand_1_out, nand_2_out;

  nand nand_1 (nand_1_out, D, En);
  nand nand_2 (nand_2_out, En, nand_1_out);
  nand nand_3 (out_3, nand_1_out, out_4);
  nand nand_4 (out_4, out_3, nand_2_out);
endmodule
