// Logisim project 5-10.circ as structural Verilog: 5 circuits, main circuit main
module main (
  input  x,
  input  y,
  output z
);

  wire and_1_out, and_2_out, and_3_out, and_4_out, and_5_out, and_6_out, and_7_out, jk_flip_flop_1_out_5,
       jk_flip_flop_1_out_6, jk_flip_flop_2_out_5, jk_flip_flop_2_out_6, not_1_out, not_2_out, or_1_out,
       or_2_out;

  not not_1 (not_1_out, x);
  not not_2 (not_2_out, y);
  and and_1 (and_1_out, x, jk_flip_flop_2_out_5);
  and and_2 (and_2_out, not_2_out, jk_flip_flop_2_out_6);
  and and_3 (and_3_out, x, not_2_out, jk_flip_flop_2_out_6);
  and and_4 (and_4_out, x, jk_flip_flop_1_out_6);
  and and_5 (and_5_out, x, not_2_out);
  or or_1 (or_1_out, and_1_out, and_2_out);
  or or_2 (or_2_out, jk_flip_flop_1_out_5, and_5_out);
  JK_Flip_Flop jk_flip_flop_1 (
    .in_1(or_1_out), .out_5(jk_flip_flop_1_out_5), .in_4(and_3_out), .out_6(jk_flip_flop_1_out_6));  // open: in_2, in_3
  JK_Flip_Flop jk_flip_flop_2 (
    .in_1(and_4_out), .out_5(jk_flip_flop_2_out_5), .in_4(or_2_out), .out_6(jk_flip_flop_2_out_6));  // open: in_2, in_3
  and and_6 (and_6_out, jk_flip_flop_1_out_5, not_1_out, not_2_out);
  and and_7 (and_7_out, jk_flip_flop_2_out_5, not_1_out, not_2_out);
  or or_3 (z, and_6_out, and_7_out);

  // Notes on the sheet:
  //   Logic Diagram ex 5-10
  //   Example of mealy machine
  //   A
  //   A'
  //   B
  //   B'
endmodule

module _8X1_MUX (
  input  in_1,
  input  in_2,
  input  in_3,
  input  in_4,
  input  in_5,
  input  in_6,
  input  in_7,
  input  in_8,
  input  in_9,
  input  in_10,
  input  in_11,
  output out_12
);
endmodule

module _2X1_MUL (
  input  in_1,
  input  in_2,
  input  in_3,
  output out_4
);
endmodule

module _4X1_MUX (
  input  in_1,
  input  in_2,
  input  in_3,
  input  in_4,
  input  in_5,
  input  in_6,
  output out_7
);
endmodule

module JK_Flip_Flop (
  input  in_1,
  input  in_2,
  input  in_3,
  input  in_4,
  output out_5,
  output out_6
);
endmodule
