// Logisim project 5-2.circ as structural Verilog: 5 circuits, main circuit main
module main (
  input  J,
  input  K,
  input  Clk,
  input  Rst
);

  wire d_flip_flop_1_out_4, n2x1_mul_1_out_4, not_1_out;

  not not_1 (not_1_out, K);
  _2X1_MUL u_2x1_mul_1 (.in_1(d_flip_flop_1_out_4), .in_2(J), .in_3(not_1_out), .out_4(n2x1_mul_1_out_4));
  D_Flip_Flop d_flip_flop_1 (.in_1(n2x1_mul_1_out_4), .in_2(Clk), .out_4(d_flip_flop_1_out_4), .in_3(Rst));

  // Notes on the sheet:
  //   JK FLIP FLOP USING D FLIP FLOP AND 2X1 MUX
endmodule

module _8X1_MUX (
  input  in_1,
  input  in_2,
  input  in_3,
  input  in_4,
  input  in_5,
  input  in_6,
  input  in_7,
  input  in_8,
  input  in_9,
  input  in_10,
  input  in_11,
  output out_12
);
endmodule

module _2X1_MUL (
  input  in_1,
  input  in_2,
  input  in_3,
  output out_4
);
endmodule

module _4X1_MUX (
  input  in_1,
  input  in_2,
  input  in_3,
  input  in_4,
  input  in_5,
  input  in_6,
  output out_7
);
endmodule

module D_Flip_Flop (
  input  in_1,
  input  in_2,
  input  in_3,
  output out_4
);
endmodule
