// Logisim project 5-31.circ as structural Verilog: 5 circuits, main circuit main
module main (
  input  A,
  input  B,
  input  C,
  input  clk,
  input  rst
);

  wire and_1_out, d_flip_flop_1_out_4, d_flip_flop_2_out_4, or_1_out;

  and and_1 (and_1_out, B, A);
  D_Flip_Flop d_flip_flop_1 (.in_1(and_1_out), .in_2(clk), .out_4(d_flip_flop_1_out_4), .in_3(rst));
  or or_1 (or_1_out, C, and_1_out);
  D_Flip_Flop d_flip_flop_2 (.in_1(or_1_out), .in_2(clk), .out_4(d_flip_flop_2_out_4), .in_3(rst));

  // Notes on the sheet:
  //   Ex 5-30
  //   E
  //   Q
endmodule

module _8X1_MUX (
  input  in_1,
  input  in_2,
  input  in_3,
  input  in_4,
  input  in_5,
  input  in_6,
  input  in_7,
  input  in_8,
  input  in_9,
  input  in_10,
  input  in_11,
  output out_12
);
endmodule

module _2X1_MUL (
  input  in_1,
  input  in_2,
  input  in_3,
  output out_4
);
endmodule

module _4X1_MUX (
  input  in_1,
  input  in_2,
  input  in_3,
  input  in_4,
  input  in_5,
  input  in_6,
  output out_7
);
endmodule

module D_Flip_Flop (
  input  in_1,
  input  in_2,
  input  in_3,
  output out_4
);
endmodule
