// Logisim project 5-56.circ as structural Verilog: 5 circuits, main circuit main
module main (
  input  Clk,
  input  Rst,
  output y2,
  output y1,
  output y0
);

  wire not_1_out, xor_1_out;

  not not_1 (not_1_out, y1);
  xor xor_1 (xor_1_out, y1, y2);
  D_Flip_Flop d_flip_flop_1 (.in_1(xor_1_out), .in_2(Clk), .out_4(y2), .in_3(Rst));
  D_Flip_Flop d_flip_flop_2 (.in_1(not_1_out), .in_2(Clk), .out_4(y1), .in_3(Rst));

  assign y0 = 1'b0;

  // Notes on the sheet:
  //   Logic diagram for exercise 5-56
  //   a
  //   b
endmodule

module _8X1_MUX (
  input  in_1,
  input  in_2,
  input  in_3,
  input  in_4,
  input  in_5,
  input  in_6,
  input  in_7,
  input  in_8,
  input  in_9,
  input  in_10,
  input  in_11,
  output out_12
);
endmodule

module _2X1_MUL (
  input  in_1,
  input  in_2,
  input  in_3,
  output out_4
);
endmodule

module _4X1_MUX (
  input  in_1,
  input  in_2,
  input  in_3,
  input  in_4,
  input  in_5,
  input  in_6,
  output out_7
);
endmodule

module D_Flip_Flop (
  input  in_1,
  input  in_2,
  input  in_3,
  output out_4
);
endmodule
