// Logisim project 5-6.circ as structural Verilog: 5 circuits, main circuit main
module main (
  input  Clk,
  input  Rst,
  input  x,
  input  y,
  output z
);

  wire and_1_out, and_2_out, and_3_out, d_flip_flop_1_out_4, not_1_out, or_1_out, or_2_out;

  not not_1 (not_1_out, x);
  and and_1 (and_1_out, not_1_out, y);
  and and_2 (and_2_out, d_flip_flop_1_out_4, x);
  or or_1 (or_1_out, and_1_out, and_2_out);
  and and_3 (and_3_out, z, not_1_out);
  or or_2 (or_2_out, and_2_out, and_3_out);
  D_Flip_Flop d_flip_flop_1 (.in_1(or_1_out), .out_4(d_flip_flop_1_out_4));  // open: in_2, in_3
  D_Flip_Flop d_flip_flop_2 (.in_1(or_2_out), .out_4(z));  // open: in_2, in_3

  // Notes on the sheet:
  //   JK FLIP FLOP USING D FLIP FLOP AND 2X1 MUX
  //   A
  //   B
endmodule

module _8X1_MUX (
  input  in_1,
  input  in_2,
  input  in_3,
  input  in_4,
  input  in_5,
  input  in_6,
  input  in_7,
  input  in_8,
  input  in_9,
  input  in_10,
  input  in_11,
  output out_12
);
endmodule

module _2X1_MUL (
  input  in_1,
  input  in_2,
  input  in_3,
  output out_4
);
endmodule

module _4X1_MUX (
  input  in_1,
  input  in_2,
  input  in_3,
  input  in_4,
  input  in_5,
  input  in_6,
  output out_7
);
endmodule

module D_Flip_Flop (
  input  in_1,
  input  in_2,
  input  in_3,
  output out_4
);
endmodule
