// Logisim project 6-10.circ as structural Verilog: 1 circuit, main circuit main
module main (
  input  [3:0] Input,
  input  Load,
  input  Shift,
  input  Clear,
  output Output
);

  wire adder_1_cout, clock_1_out, d_ff_1_q, not_1_out, shift_register_1_out;

  Clock clock_1 (.out(clock_1_out));
  Shift_Register #(.length(4)) shift_register_1 (
    .shift(Shift), .in(Output), .clk(clock_1_out), .out(shift_register_1_out), .load(Load), .clr(Clear),
    .d0(Input[3]), .d1(Input[2]), .d2(Input[1]), .d3(Input[0]));  // open: q0, q1, q2, q3
  not not_1 (not_1_out, shift_register_1_out);
  Adder #(.width(1)) adder_1 (.a(not_1_out), .b(d_ff_1_q), .out(Output), .cout(adder_1_cout));  // open: cin
  D_Flip_Flop d_ff_1 (
    .clk(clock_1_out), .D(adder_1_cout), .Q(d_ff_1_q), .preset(Clear), .en(1'b1), .reset(1'b0));  // open: Qn

  // Notes on the sheet:
  //   Clk
  //   Problem Ex 6-10
  //   2's Complementer with shift register
endmodule
