// Logisim project 6-11.circ as structural Verilog: 1 circuit, main circuit main
module main (
  input  Reset,
  input  Reset_2,
  output out_3,
  output out_4,
  output out_5,
  output out_6,
  output out_7,
  output out_8
);

  wire clock_1_out, clock_2_out, d_ff_1_qn, d_ff_2_qn, d_ff_3_qn, d_ff_4_qn, d_ff_5_qn, d_ff_6_qn;

  Clock clock_1 (.out(clock_1_out));
  Clock clock_2 (.out(clock_2_out));
  D_Flip_Flop d_ff_1 (
    .clk(clock_1_out), .D(d_ff_1_qn), .Q(out_3), .Qn(d_ff_1_qn), .preset(1'b0), .en(1'b1), .reset(Reset));
  D_Flip_Flop d_ff_2 (.clk(out_3), .D(d_ff_2_qn), .Q(out_4), .Qn(d_ff_2_qn), .preset(1'b0), .en(1'b1), .reset(Reset));
  D_Flip_Flop d_ff_3 (.clk(out_4), .D(d_ff_3_qn), .Q(out_5), .Qn(d_ff_3_qn), .preset(1'b0), .en(1'b1), .reset(Reset));
  D_Flip_Flop d_ff_4 (
    .clk(clock_2_out), .D(d_ff_4_qn), .Q(out_6), .Qn(d_ff_4_qn), .preset(1'b0), .en(1'b1), .reset(Reset_2));
  D_Flip_Flop d_ff_5 (
    .clk(d_ff_4_qn), .D(d_ff_5_qn), .Q(out_7), .Qn(d_ff_5_qn), .preset(1'b0), .en(1'b1), .reset(Reset_2));
  D_Flip_Flop d_ff_6 (
    .clk(d_ff_5_qn), .D(d_ff_6_qn), .Q(out_8), .Qn(d_ff_6_qn), .preset(1'b0), .en(1'b1), .reset(Reset_2));

  // Notes on the sheet:
  //   Ex 6-11 (a)
  //   Ex 6-11 (b)
  //   Down Counter
  //   Up Counter
endmodule
