// Logisim project 6-12.circ as structural Verilog: 1 circuit, main circuit main
module main (
  input  Reset,
  input  Reset_2,
  output [3:0] out_3,
  output [3:0] out_4
);

  wire and_1_out, and_2_out, and_3_out, and_4_out, Clk_2_out, Clk_out, t_ff_1_qn, t_ff_2_qn, t_ff_3_qn, x_qn,
       y_qn, z_qn;

  Clock Clk (.out(Clk_out));
  Clock Clk_2 (.out(Clk_2_out));
  J_K_Flip_Flop z (.J(1'b1), .clk(Clk_out), .K(1'b1), .Q(out_3[0]), .Qn(z_qn), .preset(1'b0), .en(1'b1), .reset(Reset));
  J_K_Flip_Flop y (.J(z_qn), .clk(Clk_out), .K(z_qn), .Q(out_3[1]), .Qn(y_qn), .preset(1'b0), .en(1'b1), .reset(Reset));
  J_K_Flip_Flop x (
    .J(and_1_out), .clk(Clk_out), .K(and_1_out), .Q(out_3[2]), .Qn(x_qn), .preset(1'b0), .en(1'b1),
    .reset(Reset));
  J_K_Flip_Flop w (
    .J(and_2_out), .clk(Clk_out), .K(and_2_out), .Q(out_3[3]), .preset(1'b0), .en(1'b1), .reset(Reset));  // open: Qn
  T_Flip_Flop t_ff_1 (
    .clk(Clk_2_out), .T(1'b1), .Q(out_4[0]), .Qn(t_ff_1_qn), .preset(1'b0), .reset(Reset_2), .en(1'b1));
  T_Flip_Flop t_ff_2 (
    .clk(Clk_2_out), .T(t_ff_1_qn), .Q(out_4[1]), .Qn(t_ff_2_qn), .preset(1'b0), .reset(Reset_2), .en(1'b1));
  T_Flip_Flop t_ff_3 (
    .clk(Clk_2_out), .T(and_3_out), .Q(out_4[2]), .Qn(t_ff_3_qn), .preset(1'b0), .reset(Reset_2), .en(1'b1));
  T_Flip_Flop t_ff_4 (
    .clk(Clk_2_out), .T(and_4_out), .Q(out_4[3]), .preset(1'b0), .reset(Reset_2), .en(1'b1));  // open: Qn
  and and_1 (and_1_out, z_qn, y_qn);
  and and_2 (and_2_out, z_qn, y_qn, x_qn);
  and and_3 (and_3_out, t_ff_1_qn, t_ff_2_qn);
  and and_4 (and_4_out, t_ff_1_qn, t_ff_2_qn, t_ff_3_qn);

  // Notes on the sheet:
  //   Ex 6-12(a) Down Counter using JK Flip Flop
  //   Ex 6-12(b) Down Counter using T Flip Flop
endmodule
