// Logisim project 6-13.circ as structural Verilog: 1 circuit, main circuit main
module main (
  input  Reset,
  output [3:0] Output
);

  wire and_1_out, Clk_out, d_ff_1_qn, d_ff_2_qn, d_ff_3_qn, d_ff_4_qn, or_1_out, or_2_out, or_3_out, or_4_out;

  Clock Clk (.out(Clk_out));
  or or_1 (or_1_out, Reset, and_1_out);
  or or_2 (or_2_out, Reset, and_1_out);
  or or_3 (or_3_out, Reset, and_1_out);
  or or_4 (or_4_out, Reset, and_1_out);
  D_Flip_Flop #(.trigger("falling")) d_ff_1 (
    .clk(Clk_out), .D(d_ff_1_qn), .Q(Output[0]), .Qn(d_ff_1_qn), .preset(1'b0), .en(1'b1), .reset(or_1_out));
  D_Flip_Flop #(.trigger("falling")) d_ff_2 (
    .clk(Output[0]), .D(d_ff_2_qn), .Q(Output[1]), .Qn(d_ff_2_qn), .preset(1'b0), .en(1'b1), .reset(or_2_out));
  D_Flip_Flop #(.trigger("falling")) d_ff_3 (
    .clk(Output[1]), .D(d_ff_3_qn), .Q(Output[2]), .Qn(d_ff_3_qn), .preset(1'b0), .en(1'b1), .reset(or_3_out));
  D_Flip_Flop #(.trigger("falling")) d_ff_4 (
    .clk(Output[2]), .D(d_ff_4_qn), .Q(Output[3]), .Qn(d_ff_4_qn), .preset(1'b0), .en(1'b1), .reset(or_4_out));
  and and_1 (and_1_out, Output[3], Output[1]);

  // Notes on the sheet:
  //   Ex 6-13 Ripple BCD Counter
endmodule
