// Logisim project 6-16.circ as structural Verilog: 1 circuit, main circuit main
module main (
  input  Reset,
  input  Set_Q1,
  input  Set_Q2,
  input  Set_Q4,
  input  Set_Q8,
  output [3:0] out_6
);

  wire and_1_out, Clk_out, Q8_qn;

  Clock Clk (.out(Clk_out));
  and and_1 (and_1_out, out_6[1], out_6[2]);
  J_K_Flip_Flop #(.trigger("falling")) Q1 (
    .J(1'b1), .clk(Clk_out), .K(1'b1), .Q(out_6[0]), .preset(Set_Q1), .en(1'b1), .reset(Reset));  // open: Qn
  J_K_Flip_Flop #(.trigger("falling")) Q2 (
    .J(Q8_qn), .clk(out_6[0]), .K(1'b1), .Q(out_6[1]), .preset(Set_Q2), .en(1'b1), .reset(Reset));  // open: Qn
  J_K_Flip_Flop #(.trigger("falling")) Q4 (
    .J(1'b1), .clk(out_6[1]), .K(1'b1), .Q(out_6[2]), .preset(Set_Q4), .en(1'b1), .reset(Reset));  // open: Qn
  J_K_Flip_Flop #(.trigger("falling")) Q8 (
    .J(and_1_out), .clk(out_6[0]), .K(1'b1), .Q(out_6[3]), .Qn(Q8_qn), .preset(Set_Q8), .en(1'b1),
    .reset(Reset));

  // Notes on the sheet:
  //   Ex 6-16 BCD Ripple Counter
endmodule
