// Logisim project 6-17.circ as structural Verilog: 1 circuit, main circuit main
module main (
  input  Reset,
  output [3:0] out_2
);

  wire A1_qn, and_1_out, and_2_out, clock_1_out, xor_1_out, xor_2_out, xor_3_out;

  Clock clock_1 (.out(clock_1_out));
  D_Flip_Flop A1 (.clk(clock_1_out), .D(A1_qn), .Q(out_2[0]), .Qn(A1_qn), .preset(1'b0), .en(1'b1), .reset(Reset));
  D_Flip_Flop A2 (.clk(clock_1_out), .D(xor_1_out), .Q(out_2[1]), .preset(1'b0), .en(1'b1), .reset(Reset));  // open: Qn
  D_Flip_Flop A4 (.clk(clock_1_out), .D(xor_2_out), .Q(out_2[2]), .preset(1'b0), .en(1'b1), .reset(Reset));  // open: Qn
  D_Flip_Flop A8 (.clk(clock_1_out), .D(xor_3_out), .Q(out_2[3]), .preset(1'b0), .en(1'b1), .reset(Reset));  // open: Qn
  and and_1 (and_1_out, out_2[0], out_2[1]);
  and and_2 (and_2_out, out_2[1], out_2[0], out_2[2]);
  xor xor_1 (xor_1_out, out_2[0], out_2[1]);
  xor xor_2 (xor_2_out, out_2[2], and_1_out);
  xor xor_3 (xor_3_out, out_2[3], and_2_out);

  // Notes on the sheet:
  //   Ex 6-17. 4 Bit counter using D-Flip Flop
endmodule
