// Logisim project 6-18.circ as structural Verilog: 1 circuit, main circuit main
module main (
  input  Down,
  input  Up,
  input  Clear,
  output [3:0] out_4
);

  wire and_1_out, and_2_out, and_3_out, and_4_out, and_5_out, and_6_out, and_7_out, and_8_out, Clk_out,
       not_1_out, not_2_out, or_1_out, or_2_out, or_3_out, or_4_out, t_ff_1_qn, t_ff_2_qn, t_ff_3_qn;

  Clock Clk (.out(Clk_out));
  not not_1 (not_1_out, Down);
  not not_2 (not_2_out, Up);
  and and_1 (and_1_out, Up, not_1_out);
  and and_2 (and_2_out, Down, not_2_out);
  and and_3 (and_3_out, and_1_out, out_4[0]);
  and and_4 (and_4_out, and_2_out, t_ff_1_qn);
  and and_5 (and_5_out, and_4_out, t_ff_2_qn);
  and and_6 (and_6_out, and_3_out, out_4[1]);
  and and_7 (and_7_out, and_6_out, out_4[2]);
  and and_8 (and_8_out, and_5_out, t_ff_3_qn);
  or or_1 (or_1_out, and_1_out, and_2_out);
  or or_2 (or_2_out, and_3_out, and_4_out);
  or or_3 (or_3_out, and_6_out, and_5_out);
  or or_4 (or_4_out, and_7_out, and_8_out);
  T_Flip_Flop t_ff_1 (
    .clk(Clk_out), .T(or_1_out), .Q(out_4[0]), .Qn(t_ff_1_qn), .preset(1'b0), .reset(Clear), .en(1'b1));
  T_Flip_Flop t_ff_2 (
    .clk(Clk_out), .T(or_2_out), .Q(out_4[1]), .Qn(t_ff_2_qn), .preset(1'b0), .reset(Clear), .en(1'b1));
  T_Flip_Flop t_ff_3 (
    .clk(Clk_out), .T(or_3_out), .Q(out_4[2]), .Qn(t_ff_3_qn), .preset(1'b0), .reset(Clear), .en(1'b1));
  T_Flip_Flop t_ff_4 (.clk(Clk_out), .T(or_4_out), .Q(out_4[3]), .preset(1'b0), .reset(Clear), .en(1'b1));  // open: Qn

  // Notes on the sheet:
  //   Ex 6-18 Up Down Binary Synchronous Counter
endmodule
