// Logisim project 6-2.circ as structural Verilog: 5 circuits, main circuit main
module main (
  input  Load,
  input  Reset,
  input  I3,
  input  I2,
  input  I1,
  input  I0
);

  wire and_1_out, and_2_out, and_3_out, and_4_out, and_5_out, and_6_out, and_7_out, and_8_out, clock_1_out,
       d_flip_flop_1_out_4, d_flip_flop_2_out_4, d_flip_flop_3_out_4, d_flip_flop_4_out_4, not_1_out,
       not_2_out, or_1_out, or_2_out, or_3_out, or_4_out;

  not not_1 (not_1_out, Load);
  not not_2 (not_2_out, Reset);
  Clock clock_1 (.out(clock_1_out));
  and and_1 (and_1_out, I0, Load);
  and and_2 (and_2_out, not_1_out, not_2_out, d_flip_flop_1_out_4);
  and and_3 (and_3_out, I1, Load);
  and and_4 (and_4_out, not_1_out, not_2_out, d_flip_flop_2_out_4);
  and and_5 (and_5_out, I2, Load);
  and and_6 (and_6_out, not_1_out, not_2_out, d_flip_flop_3_out_4);
  and and_7 (and_7_out, I3, Load);
  and and_8 (and_8_out, not_1_out, not_2_out, d_flip_flop_4_out_4);
  or or_1 (or_1_out, and_1_out, and_2_out);
  or or_2 (or_2_out, and_3_out, and_4_out);
  or or_3 (or_3_out, and_5_out, and_6_out);
  or or_4 (or_4_out, and_7_out, and_8_out);
  D_Flip_Flop d_flip_flop_1 (.in_1(or_1_out), .in_2(clock_1_out), .out_4(d_flip_flop_1_out_4), .in_3(1'b1));
  D_Flip_Flop d_flip_flop_2 (.in_1(or_2_out), .in_2(clock_1_out), .out_4(d_flip_flop_2_out_4), .in_3(1'b1));
  D_Flip_Flop d_flip_flop_3 (.in_1(or_3_out), .in_2(clock_1_out), .out_4(d_flip_flop_3_out_4), .in_3(1'b1));
  D_Flip_Flop d_flip_flop_4 (.in_1(or_4_out), .in_2(clock_1_out), .out_4(d_flip_flop_4_out_4), .in_3(1'b1));

  // Notes on the sheet:
  //   Logic diagram for exercise 6-2
  //   Clk
  //   Register with synchronous reset
  //   A0
  //   A1
  //   A2
  //   A3
endmodule

module _8X1_MUX (
  input  in_1,
  input  in_2,
  input  in_3,
  input  in_4,
  input  in_5,
  input  in_6,
  input  in_7,
  input  in_8,
  input  in_9,
  input  in_10,
  input  in_11,
  output out_12
);
endmodule

module _2X1_MUL (
  input  in_1,
  input  in_2,
  input  in_3,
  output out_4
);
endmodule

module _4X1_MUX (
  input  in_1,
  input  in_2,
  input  in_3,
  input  in_4,
  input  in_5,
  input  in_6,
  output out_7
);
endmodule

module D_Flip_Flop (
  input  in_1,
  input  in_2,
  input  in_3,
  output out_4
);
endmodule
