// Logisim project 6-20.circ as structural Verilog: 1 circuit, main circuit main
module main (
  input  Reset,
  input  Count,
  input  Load,
  input  [3:0] Input,
  output [7:0] Current_Count
);

  wire _3_0_carry, Clk_out;

  Clock Clk (.out(Clk_out));
  Counter #(.width(4), .max('hf)) _3_0 (
    .load(Current_Count[6]), .D(Input), .count(Count), .Q(Current_Count[3:0]), .carry(_3_0_carry),
    .clk(Clk_out), .clr(Reset));
  Counter #(.width(4), .max('hf)) _7_4 (
    .load(Current_Count[6]), .D(Input), .count(_3_0_carry), .Q(Current_Count[7:4]), .clk(Clk_out), .clr(Reset));  // open: carry
endmodule
