// Logisim project 6-22.circ as structural Verilog: 2 circuits, main circuit main
module main (
);

  wire and_1_out, counter_1_out_10, counter_1_out_11, counter_1_out_12, counter_1_out_13, counter_2_out_10,
       counter_2_out_11, counter_2_out_12, counter_2_out_13, counter_3_out_10, counter_3_out_11,
       counter_3_out_12, counter_3_out_13, nand_1_out, not_1_out, undriven, undriven_2, undriven_3,
       undriven_4, undriven_5, undriven_6, undriven_7, undriven_8, undriven_9, undriven_10, undriven_11,
       undriven_12;

  Counter counter_1 (
    .in_2(undriven), .in_3(undriven_9), .in_4(undriven_8), .in_5(undriven_7), .in_6(and_1_out), .in_7(1'b0),
    .in_8(1'b0), .in_9(1'b0), .out_10(counter_1_out_10), .out_11(counter_1_out_11),
    .out_12(counter_1_out_12), .out_13(counter_1_out_13), .in_1(1'b0));
  Counter counter_2 (
    .in_2(undriven_3), .in_3(undriven_6), .in_4(undriven_5), .in_5(undriven_4), .in_6(undriven_3),
    .in_7(1'b0), .in_8(1'b0), .in_9(1'b1), .out_10(counter_2_out_10), .out_11(counter_2_out_11),
    .out_12(counter_2_out_12), .out_13(counter_2_out_13), .in_1(1'b0));
  Counter counter_3 (
    .in_2(undriven_2), .in_3(not_1_out), .in_4(undriven_12), .in_5(undriven_11), .in_6(undriven_10),
    .in_7(1'b0), .in_8(1'b0), .in_9(1'b0), .out_10(counter_3_out_10), .out_11(counter_3_out_11),
    .out_12(counter_3_out_12), .out_13(counter_3_out_13), .in_1(1'b0));
  not not_1 (not_1_out, nand_1_out);
  and and_1 (and_1_out, counter_1_out_10, counter_1_out_12, counter_1_out_13);
  nand nand_1 (nand_1_out, counter_3_out_11, counter_3_out_10);

  // Notes on the sheet:
  //   c_out
  //   c_out
  //   parallel output
  //   parallel Input
  //   parallel output
  //   parallel Input
  //   c_out
  //   (a) Mod-12 counter using And gate and load input
  //   (b) Mod-12 counter using carry output
  //   (b) Mod-12 counter using NAND gate and asynchronous clear input
  //   parallel output
  //   parallel Input
  //   Load
  //   Load
  //   Load
  //   Count = 1
  //   Clk
  //   Reset = 1
  //   Count = 1
  //   Clk
  //   Reset = 1
  //   Clk
  //   Reset
  //   Load = 0
  //   Count = 1
endmodule

module Counter (
  input  in_1,
  input  in_2,
  input  in_3,
  input  in_4,
  input  in_5,
  input  in_6,
  input  in_7,
  input  in_8,
  input  in_9,
  output out_10,
  output out_11,
  output out_12,
  output out_13
);
endmodule
