// Logisim project 6-24.circ as structural Verilog: 1 circuit, main circuit main
module main (
  input  Px,
  input  Py,
  input  Pz,
  input  Rx,
  input  Ry,
  input  Rz,
  output x,
  output y,
  output z
);

  wire and_1_out, and_2_out, and_3_out, and_4_out, and_5_out, Clk_out, or_1_out, or_2_out, or_3_out, x_qn,
       y_qn, z_qn;

  Clock Clk (.out(Clk_out));
  T_Flip_Flop u_x (.clk(Clk_out), .T(or_1_out), .Q(x), .Qn(x_qn), .preset(Px), .reset(Rx), .en(1'b1));
  T_Flip_Flop u_y (.clk(Clk_out), .T(or_2_out), .Q(y), .Qn(y_qn), .preset(Py), .reset(Ry), .en(1'b1));
  T_Flip_Flop u_z (.clk(Clk_out), .T(or_3_out), .Q(z), .Qn(z_qn), .preset(Pz), .reset(Rz), .en(1'b1));
  or or_1 (or_1_out, and_2_out, and_1_out);
  and and_1 (and_1_out, x, y_qn);
  and and_2 (and_2_out, y_qn, z);
  or or_2 (or_2_out, and_3_out, x_qn);
  and and_3 (and_3_out, y, z_qn);
  or or_3 (or_3_out, and_4_out, and_5_out);
  and and_4 (and_4_out, x, z);
  and and_5 (and_5_out, x_qn, z_qn);
endmodule
