// Logisim project 6-25.circ as structural Verilog: 1 circuit, main circuit main
module main (
  input  Shift,
  input  Clear,
  input  Load,
  input  [5:0] Init_Value,
  output [5:0] out_5
);

  wire Clk_out, decoder_1_out0, decoder_1_out1, decoder_1_out2, decoder_1_out3, decoder_1_out4,
       decoder_1_out5, shift_register_1_out;
  wire [2:0] counter_1_q;

  Clock Clk (.out(Clk_out));
  Counter #(.width(3), .max('h7)) counter_1 (.Q(counter_1_q));  // open: load, D, count, carry, clk, clr
  Decoder #(.select(3)) decoder_1 (
    .out0(decoder_1_out0), .out1(decoder_1_out1), .out2(decoder_1_out2), .out3(decoder_1_out3),
    .out4(decoder_1_out4), .out5(decoder_1_out5), .sel(counter_1_q));  // open: out6, out7, en
  Shift_Register #(.length(6)) shift_register_1 (
    .shift(Shift), .in(shift_register_1_out), .clk(Clk_out), .out(shift_register_1_out), .load(Load),
    .clr(Clear), .d0(Init_Value[0]), .q0(out_5[0]), .d1(Init_Value[1]), .q1(out_5[1]), .d2(Init_Value[2]),
    .q2(out_5[2]), .d3(Init_Value[3]), .q3(out_5[3]), .d4(Init_Value[4]), .q4(out_5[4]), .d5(Init_Value[5]),
    .q5(out_5[5]));

  // Notes on the sheet:
  //   6-25 (a)
  //   6-25 (b)
  //   3 bits
  //   Counter
  //   Decoder
endmodule
