// Logisim project 6-27.circ as structural Verilog: 1 circuit, main circuit main
module main (
  input  reset,
  output [2:0] out_2
);

  wire and_1_out, Clk_out, or_1_out, x_qn, y_qn;

  Clock Clk (.out(Clk_out));
  or or_1 (or_1_out, out_2[2], out_2[0]);
  and and_1 (and_1_out, out_2[1], x_qn);
  J_K_Flip_Flop x (.J(y_qn), .clk(Clk_out), .K(1'b1), .Q(out_2[2]), .Qn(x_qn), .preset(1'b0), .en(1'b1), .reset(reset));
  J_K_Flip_Flop y (
    .J(or_1_out), .clk(Clk_out), .K(1'b1), .Q(out_2[1]), .Qn(y_qn), .preset(1'b0), .en(1'b1), .reset(reset));
  J_K_Flip_Flop z (
    .J(and_1_out), .clk(Clk_out), .K(1'b1), .Q(out_2[0]), .preset(1'b0), .en(1'b1), .reset(reset));  // open: Qn

  // Notes on the sheet:
  //   ex 6-27
endmodule
