// Logisim project 6-28.circ as structural Verilog
module _6_28_a (
  input  reset,
  output [2:0] out_2
);

  wire and_1_out, and_2_out, Clk_out, or_1_out, x_qn, xor_1_out, y_qn, z_qn;

  Clock Clk (.out(Clk_out));
  or or_1 (or_1_out, out_2[0], and_1_out);
  xor xor_1 (xor_1_out, out_2[1], out_2[2]);
  D_Flip_Flop x (.clk(Clk_out), .D(xor_1_out), .Q(out_2[2]), .Qn(x_qn), .preset(1'b0), .en(1'b1), .reset(reset));
  and and_1 (and_1_out, out_2[2], y_qn);
  D_Flip_Flop y (.clk(Clk_out), .D(or_1_out), .Q(out_2[1]), .Qn(y_qn), .preset(1'b0), .en(1'b1), .reset(reset));
  and and_2 (and_2_out, x_qn, y_qn, z_qn);
  D_Flip_Flop z (.clk(Clk_out), .D(and_2_out), .Q(out_2[0]), .Qn(z_qn), .preset(1'b0), .en(1'b1), .reset(reset));
endmodule

module _6_28_b (
  input  reset,
  output [2:0] out_2
);

  wire and_1_out, and_2_out, and_3_out, and_4_out, and_5_out, and_6_out, and_7_out, Clk_out, or_1_out,
       or_2_out, or_3_out;

  Clock Clk (.out(Clk_out));
  or or_1 (or_1_out, and_1_out, and_2_out);
  or or_2 (or_2_out, and_3_out, and_4_out);
  or or_3 (or_3_out, and_5_out, and_6_out, and_7_out);
  // AND_Gate and_1 has open pins: out=and_1_out
  // AND_Gate and_2 has open pins: out=and_2_out
  D_Flip_Flop x (.clk(Clk_out), .D(or_1_out), .Q(out_2[2]), .preset(1'b0), .en(1'b1), .reset(reset));  // open: Qn
  // AND_Gate and_3 has open pins: out=and_3_out
  // AND_Gate and_4 has open pins: out=and_4_out
  D_Flip_Flop y (.clk(Clk_out), .D(or_2_out), .Q(out_2[1]), .preset(1'b0), .en(1'b1), .reset(reset));  // open: Qn
  and and_5 (and_5_out, out_2[1], out_2[0]);
  and and_6 (and_6_out, out_2[2], out_2[0]);
  and and_7 (and_7_out, out_2[1], out_2[2]);
  D_Flip_Flop z (.clk(Clk_out), .D(or_3_out), .Q(out_2[0]), .preset(1'b0), .en(1'b1), .reset(reset));  // open: Qn
endmodule
