// Logisim project 6-29.circ as structural Verilog
module switch_tail_counter (
  input  reset,
  output out_2,
  output out_3,
  output out_4,
  output out_5,
  output out_6,
  output out_7,
  output out_8,
  output out_9
);

  wire A_q, A_qn, B_q, B_qn, C_q, C_qn, Clk_out, E_q, E_qn;

  Clock Clk (.out(Clk_out));
  and and_1 (out_2, A_qn, E_qn);
  and and_2 (out_3, A_q, B_qn);
  and and_3 (out_5, C_q, E_qn);
  and and_4 (out_4, B_q, C_qn);
  D_Flip_Flop A (.clk(Clk_out), .D(E_qn), .Q(A_q), .Qn(A_qn), .preset(1'b0), .en(1'b1), .reset(reset));
  and and_5 (out_7, A_qn, B_q);
  and and_6 (out_6, A_q, E_q);
  D_Flip_Flop B (.clk(Clk_out), .D(A_q), .Q(B_q), .Qn(B_qn), .preset(1'b0), .en(1'b1), .reset(reset));
  and and_7 (out_8, B_qn, C_q);
  and and_8 (out_9, C_qn, E_q);
  D_Flip_Flop C (.clk(Clk_out), .D(B_q), .Q(C_q), .Qn(C_qn), .preset(1'b0), .en(1'b1), .reset(reset));
  D_Flip_Flop E (.clk(Clk_out), .D(C_q), .Q(E_q), .Qn(E_qn), .preset(1'b0), .en(1'b1), .reset(reset));

  // Notes on the sheet:
  //   Switch Tail Counter
endmodule

module switch_tail_counter_unstable (
  input  reset,
  input  Set_A,
  input  Set_B,
  input  Set_C,
  input  Set_E,
  output out_6,
  output out_7,
  output out_8,
  output out_9,
  output out_10,
  output out_11,
  output out_12,
  output out_13
);

  wire A_q, A_qn, B_q, B_qn, C_q, C_qn, Clk_out, E_q, E_qn;

  Clock Clk (.out(Clk_out));
  and and_1 (out_6, A_qn, E_qn);
  and and_2 (out_7, A_q, B_qn);
  and and_3 (out_8, B_q, C_qn);
  and and_4 (out_9, C_q, E_qn);
  D_Flip_Flop A (.clk(Clk_out), .D(E_qn), .Q(A_q), .Qn(A_qn), .preset(Set_A), .en(1'b1), .reset(reset));
  and and_5 (out_11, A_qn, B_q);
  and and_6 (out_10, A_q, E_q);
  D_Flip_Flop B (.clk(Clk_out), .D(A_q), .Q(B_q), .Qn(B_qn), .preset(Set_B), .en(1'b1), .reset(reset));
  and and_7 (out_13, C_qn, E_q);
  and and_8 (out_12, B_qn, C_q);
  D_Flip_Flop C (.clk(Clk_out), .D(B_q), .Q(C_q), .Qn(C_qn), .preset(Set_C), .en(1'b1), .reset(reset));
  D_Flip_Flop E (.clk(Clk_out), .D(C_q), .Q(E_q), .Qn(E_qn), .preset(Set_E), .en(1'b1), .reset(reset));

  // Notes on the sheet:
  //   Switch Tail Counter
endmodule

module switch_tali_counter_corrected (
  input  reset,
  input  Set_A,
  input  Set_B,
  input  Set_C,
  input  Set_E,
  output out_6,
  output out_7,
  output out_8,
  output out_9,
  output out_10,
  output out_11,
  output out_12,
  output out_13
);

  wire A_q, A_qn, and_9_out, B_q, B_qn, C_q, C_qn, Clk_out, E_q, E_qn, or_1_out;

  Clock Clk (.out(Clk_out));
  and and_1 (out_7, A_q, B_qn);
  and and_2 (out_6, A_qn, E_qn);
  and and_3 (out_8, B_q, C_qn);
  and and_4 (out_9, C_q, E_qn);
  D_Flip_Flop A (.clk(Clk_out), .D(E_qn), .Q(A_q), .Qn(A_qn), .preset(Set_A), .en(1'b1), .reset(reset));
  and and_5 (out_11, A_qn, B_q);
  and and_6 (out_10, A_q, E_q);
  D_Flip_Flop B (.clk(Clk_out), .D(A_q), .Q(B_q), .Qn(B_qn), .preset(Set_B), .en(1'b1), .reset(reset));
  and and_7 (out_13, C_qn, E_q);
  and and_8 (out_12, B_qn, C_q);
  and and_9 (and_9_out, B_q, or_1_out);
  or or_1 (or_1_out, C_q, A_q);
  D_Flip_Flop C (.clk(Clk_out), .D(and_9_out), .Q(C_q), .Qn(C_qn), .preset(Set_C), .en(1'b1), .reset(reset));
  D_Flip_Flop E (.clk(Clk_out), .D(C_q), .Q(E_q), .Qn(E_qn), .preset(Set_E), .en(1'b1), .reset(reset));

  // Notes on the sheet:
  //   Switch Tail Counter
endmodule
