// Logisim project 6-5.circ as structural Verilog: 6 circuits, main circuit main
module main (
  input  Clk,
  input  Clear_b,
  input  MSB_in,
  input  in_4,
  input  [7:0] _3_0,
  input  [1:0] S1S0,
  output [7:0] _7_4
);

  wire undriven;

  _4_bit_Universal_Shift_register u_4_bit_universal_shift_register_1 ();  // open: Clear_b, MSB_in, in_6, in_7, in_8, A_par, Vcc, Gnd, in_3
  _4_bit_Universal_Shift_register u_4_bit_universal_shift_register_2 (
    .Clear_b(Clear_b), .MSB_in(MSB_in), .in_6(undriven), .in_7(S1S0), .in_8(_3_0[7:4]), .A_par(_7_4[7:4]),
    .Vcc(1'b1), .Gnd(1'b0), .in_3(Clk));
  _4_bit_Universal_Shift_register u_4_bit_universal_shift_register_3 (
    .Clear_b(Clear_b), .MSB_in(undriven), .in_6(in_4), .in_7(S1S0), .in_8(_3_0[3:0]), .A_par(_7_4[3:0]),
    .Vcc(1'b1), .Gnd(1'b0), .in_3(Clk));

  // Notes on the sheet:
  //   Logic diagram for ex 6-5 (a)
  //   Logic diagram for ex 6-5 (b) 8 bit universal shift register
  //   Gnd
  //   Vcc
  //   [7:4]
  //   [7:4]
  //   LSB_in
  //   A_par
  //   [7:4]
  //   I_par
  //   [3:0]
  //   [3:0]
  //   [3:0]
endmodule

module _8X1_MUX (
  input  in_1,
  input  in_2,
  input  in_3,
  input  in_4,
  input  in_5,
  input  in_6,
  input  in_7,
  input  in_8,
  input  in_9,
  input  in_10,
  input  in_11,
  output out_12
);
endmodule

module _2X1_MUL (
  input  in_1,
  input  in_2,
  input  in_3,
  output out_4
);
endmodule

module _4X1_MUX (
  input  in_1,
  input  in_2,
  input  in_3,
  input  in_4,
  input  in_5,
  input  in_6,
  output out_7
);
endmodule

module D_Flip_Flop (
  input  in_1,
  input  in_2,
  input  in_3,
  output out_4
);
endmodule

module _4_bit_Universal_Shift_register (
  input  Vcc,
  input  Gnd,
  input  in_3,
  input  Clear_b,
  input  MSB_in,
  input  in_6,
  input  [1:0] in_7,
  input  [3:0] in_8,
  output [3:0] A_par
);


  // Notes on the sheet:
  //   Clk
  //   LSB_in
  //   select
  //   I_par
endmodule
