// Logisim project 6-6.circ as structural Verilog: 6 circuits, main circuit main
module main (
  input  reset,
  input  Load,
  input  Shift,
  input  [3:0] I_Par,
  output [3:0] A_par
);

  wire clock_1_out, multiplexer_1_out, multiplexer_2_out, multiplexer_3_out, multiplexer_4_out;

  Clock clock_1 (.out(clock_1_out));
  Multiplexer #(.select(2), .enable("false")) multiplexer_1 (
    .in0(A_par[3]), .in1(I_Par[3]), .in2(A_par[0]), .in3(A_par[0]), .out(multiplexer_1_out),
    .sel({Shift, Load}));
  Multiplexer #(.select(2), .enable("false")) multiplexer_2 (
    .in0(A_par[2]), .in1(I_Par[2]), .in2(A_par[3]), .in3(A_par[3]), .out(multiplexer_2_out),
    .sel({Shift, Load}));
  Multiplexer #(.select(2), .enable("false")) multiplexer_3 (
    .in0(A_par[1]), .in1(I_Par[1]), .in2(A_par[2]), .in3(A_par[2]), .out(multiplexer_3_out),
    .sel({Shift, Load}));
  Multiplexer #(.select(2), .enable("false")) multiplexer_4 (
    .in0(A_par[0]), .in1(I_Par[0]), .in2(A_par[1]), .in3(A_par[1]), .out(multiplexer_4_out),
    .sel({Shift, Load}));
  D_Flip_Flop_part A3 (
    .clk(clock_1_out), .D(multiplexer_1_out), .Q(A_par[3]), .preset(1'b0), .en(1'b1), .reset(reset));  // open: Qn
  D_Flip_Flop_part A2 (
    .clk(clock_1_out), .D(multiplexer_2_out), .Q(A_par[2]), .preset(1'b0), .en(1'b1), .reset(reset));  // open: Qn
  D_Flip_Flop_part A1 (
    .clk(clock_1_out), .D(multiplexer_3_out), .Q(A_par[1]), .preset(1'b0), .en(1'b1), .reset(reset));  // open: Qn
  D_Flip_Flop_part A0 (
    .clk(clock_1_out), .D(multiplexer_4_out), .Q(A_par[0]), .preset(1'b0), .en(1'b1), .reset(reset));  // open: Qn

  // Notes on the sheet:
  //   Clk
  //   Logic diagram for ex 6-6
  //   4 bit shift register
endmodule

module _8X1_MUX (
  input  in_1,
  input  in_2,
  input  in_3,
  input  in_4,
  input  in_5,
  input  in_6,
  input  in_7,
  input  in_8,
  input  in_9,
  input  in_10,
  input  in_11,
  output out_12
);
endmodule

module _2X1_MUL (
  input  in_1,
  input  in_2,
  input  in_3,
  output out_4
);
endmodule

module _4X1_MUX (
  input  in_1,
  input  in_2,
  input  in_3,
  input  in_4,
  input  in_5,
  input  in_6,
  output out_7
);
endmodule

module D_Flip_Flop (
  input  in_1,
  input  in_2,
  input  in_3,
  output out_4
);
endmodule

module _4_bit_Universal_Shift_register (
  input  Vcc,
  input  Gnd,
  input  in_3,
  input  Clear_b,
  input  MSB_in,
  input  in_6,
  input  [1:0] in_7,
  input  [3:0] in_8,
  output [3:0] A_par
);


  // Notes on the sheet:
  //   Clk
  //   LSB_in
  //   select
  //   I_par
endmodule
