// Logisim project 6-7.circ as structural Verilog: 6 circuits, main circuit main
module main (
  input  reset,
  input  S0,
  input  S1,
  input  [3:0] I_Par,
  output [3:0] A_par
);

  wire A0_qn, A1_qn, A2_qn, A3_qn, clock_1_out, multiplexer_1_out, multiplexer_2_out, multiplexer_3_out,
       multiplexer_4_out;

  Clock clock_1 (.out(clock_1_out));
  Multiplexer #(.select(2), .enable("false")) multiplexer_1 (
    .in0(A_par[3]), .in1(A3_qn), .in2(1'b0), .in3(I_Par[3]), .out(multiplexer_1_out), .sel({S1, S0}));
  Multiplexer #(.select(2), .enable("false")) multiplexer_2 (
    .in0(A_par[2]), .in1(A2_qn), .in2(1'b0), .in3(I_Par[2]), .out(multiplexer_2_out), .sel({S1, S0}));
  Multiplexer #(.select(2), .enable("false")) multiplexer_3 (
    .in0(A_par[1]), .in1(A1_qn), .in2(1'b0), .in3(I_Par[1]), .out(multiplexer_3_out), .sel({S1, S0}));
  Multiplexer #(.select(2), .enable("false")) multiplexer_4 (
    .in0(A_par[0]), .in1(A0_qn), .in2(1'b0), .in3(I_Par[0]), .out(multiplexer_4_out), .sel({S1, S0}));
  D_Flip_Flop_part A3 (
    .clk(clock_1_out), .D(multiplexer_1_out), .Q(A_par[3]), .Qn(A3_qn), .preset(1'b0), .en(1'b1),
    .reset(reset));
  D_Flip_Flop_part A2 (
    .clk(clock_1_out), .D(multiplexer_2_out), .Q(A_par[2]), .Qn(A2_qn), .preset(1'b0), .en(1'b1),
    .reset(reset));
  D_Flip_Flop_part A1 (
    .clk(clock_1_out), .D(multiplexer_3_out), .Q(A_par[1]), .Qn(A1_qn), .preset(1'b0), .en(1'b1),
    .reset(reset));
  D_Flip_Flop_part A0 (
    .clk(clock_1_out), .D(multiplexer_4_out), .Q(A_par[0]), .Qn(A0_qn), .preset(1'b0), .en(1'b1),
    .reset(reset));

  // Notes on the sheet:
  //   Clk
  //   Logic diagram for ex 6-7
  //   4 bit shift register
endmodule

module _8X1_MUX (
  input  in_1,
  input  in_2,
  input  in_3,
  input  in_4,
  input  in_5,
  input  in_6,
  input  in_7,
  input  in_8,
  input  in_9,
  input  in_10,
  input  in_11,
  output out_12
);
endmodule

module _2X1_MUL (
  input  in_1,
  input  in_2,
  input  in_3,
  output out_4
);
endmodule

module _4X1_MUX (
  input  in_1,
  input  in_2,
  input  in_3,
  input  in_4,
  input  in_5,
  input  in_6,
  output out_7
);
endmodule

module D_Flip_Flop (
  input  in_1,
  input  in_2,
  input  in_3,
  output out_4
);
endmodule

module _4_bit_Universal_Shift_register (
  input  Vcc,
  input  Gnd,
  input  in_3,
  input  Clear_b,
  input  MSB_in,
  input  in_6,
  input  [1:0] in_7,
  input  [3:0] in_8,
  output [3:0] A_par
);


  // Notes on the sheet:
  //   Clk
  //   LSB_in
  //   select
  //   I_par
endmodule
