// Logisim project 7-15.circ as structural Verilog
module _64X8_Rom (
  input  i2,
  input  i1,
  input  i0,
  input  i3,
  input  address_0,
  input  address_1,
  input  Sel,
  output [7:0] out_8
);
endmodule

module Memory_Cell (
  input  Reset,
  input  Select,
  input  Input,
  input  Read_Write,
  output Output
);

  wire and_1_out, and_2_out, and_3_out, not_1_out, not_2_out, not_3_out, sr_latch_1_out_3;

  not not_1 (not_1_out, Reset);
  and and_1 (and_1_out, not_1_out, Input);
  not not_2 (not_2_out, and_1_out);
  and and_2 (and_2_out, and_1_out, not_3_out, Select);
  and and_3 (and_3_out, not_2_out, not_3_out, Select);
  not not_3 (not_3_out, Read_Write);
  SR_Latch sr_latch_1 (.Reset(and_3_out), .Set(and_2_out), .out_3(sr_latch_1_out_3));  // open: out_4
  and and_4 (Output, sr_latch_1_out_3, Select, Read_Write);

  // Notes on the sheet:
  //   Memory Cell
endmodule

module SR_Latch (
  input  Reset,
  input  Set,
  output out_3,
  output out_4
);

  nor nor_1 (out_3, Reset, out_4);
  nor nor_2 (out_4, out_3, Set);
endmodule

module _2X4_Decoder (
  input  i0,
  input  i1,
  input  sel,
  output a0,
  output a1,
  output a2,
  output a3
);

  wire not_1_out, not_2_out;

  not not_1 (not_1_out, i0);
  not not_2 (not_2_out, i1);
  and and_1 (a0, sel, not_2_out, not_1_out);
  and and_2 (a1, sel, not_2_out, i0);
  and and_3 (a3, sel, i1, i0);
  and and_4 (a2, sel, i1, not_1_out);
endmodule

module _256X8_ROM (
  input  a7,
  input  a6,
  input  a5,
  input  a4,
  input  a3,
  input  a2,
  input  a1,
  input  a0,
  output [7:0] out_9
);

  wire n2x4_decoder_1_a0, n2x4_decoder_1_a1, n2x4_decoder_1_a2, n2x4_decoder_1_a3;
  wire [7:0] n64x8_rom_1_out_8, n64x8_rom_2_out_8, n64x8_rom_3_out_8, n64x8_rom_4_out_8;

  _2X4_Decoder u_2x4_decoder_1 (
    .i0(a6), .i1(a7), .sel(1'b1), .a0(n2x4_decoder_1_a0), .a1(n2x4_decoder_1_a1), .a2(n2x4_decoder_1_a2),
    .a3(n2x4_decoder_1_a3));
  _64X8_Rom u_64x8_rom_1 (
    .address_1(a0), .Sel(a1), .address_0(n2x4_decoder_1_a0), .i0(a5), .i3(a2), .i2(a3), .i1(a4),
    .out_8(n64x8_rom_1_out_8));
  _64X8_Rom u_64x8_rom_2 (
    .address_1(a0), .Sel(a1), .address_0(n2x4_decoder_1_a1), .i0(a5), .i3(a2), .i2(a3), .i1(a4),
    .out_8(n64x8_rom_2_out_8));
  _64X8_Rom u_64x8_rom_3 (
    .address_1(a0), .Sel(a1), .address_0(n2x4_decoder_1_a2), .i0(a5), .i3(a2), .i2(a3), .i1(a4),
    .out_8(n64x8_rom_3_out_8));
  _64X8_Rom u_64x8_rom_4 (
    .address_1(a0), .Sel(a1), .address_0(n2x4_decoder_1_a3), .i0(a5), .i3(a2), .i2(a3), .i1(a4),
    .out_8(n64x8_rom_4_out_8));
  assign out_9 = n64x8_rom_1_out_8 | n64x8_rom_2_out_8 | n64x8_rom_3_out_8 | n64x8_rom_4_out_8;  // OR_Gate or_1, 8 bits wide
endmodule
