// Logisim project 7-28.circ as structural Verilog: 1 circuit, main circuit main
module main (
  input  A,
  input  B,
  input  C,
  output F2,
  output F1
);

  wire and_1_out, and_4_out, not_2_out, or_1_out, or_2_out;

  not not_1 (A, A);
  not not_2 (not_2_out, A);
  not not_3 (A, A);
  buf and_1 (and_1_out, A);  // AND_Gate
  buf and_2 (and_1_out, A);  // AND_Gate
  buf and_3 (and_1_out, A);  // AND_Gate
  buf and_4 (and_4_out, A);  // AND_Gate
  buf and_5 (and_4_out, A);  // AND_Gate
  buf and_6 (and_4_out, A);  // AND_Gate
  buf or_1 (or_1_out, and_1_out);  // OR_Gate
  buf or_2 (or_2_out, and_4_out);  // OR_Gate
  xor xor_1 (F2, 1'b1, or_2_out);
  xor xor_2 (F1, 1'b0, or_1_out);

  assign B = A;
  assign C = A;
endmodule
