// Logisim project 7-6.circ as structural Verilog
module _4X4_Ram (
  input  i2,
  input  i1,
  input  i0,
  input  i3,
  input  Reset,
  input  address_0,
  input  address_1,
  input  memory_enable,
  input  read_write,
  output a0,
  output a3,
  output a2,
  output a1
);

  wire memory_cell_1_output, memory_cell_2_output, memory_cell_3_output, memory_cell_4_output,
       memory_cell_5_output, memory_cell_6_output, memory_cell_7_output, memory_cell_8_output,
       memory_cell_9_output, memory_cell_10_output, memory_cell_11_output, memory_cell_12_output,
       memory_cell_13_output, memory_cell_14_output, memory_cell_15_output, memory_cell_16_output,
       n2x4_decoder_1_a0, n2x4_decoder_1_a1, n2x4_decoder_1_a2, n2x4_decoder_1_a3;

  _2X4_Decoder u_2x4_decoder_1 (
    .i0(address_0), .i1(address_1), .sel(memory_enable), .a0(n2x4_decoder_1_a0), .a1(n2x4_decoder_1_a1),
    .a2(n2x4_decoder_1_a2), .a3(n2x4_decoder_1_a3));
  Memory_Cell memory_cell_1 (
    .Input(i3), .Output(memory_cell_1_output), .Reset(Reset), .Select(n2x4_decoder_1_a0),
    .Read_Write(read_write));
  Memory_Cell memory_cell_2 (
    .Input(i3), .Output(memory_cell_2_output), .Reset(Reset), .Select(n2x4_decoder_1_a1),
    .Read_Write(read_write));
  Memory_Cell memory_cell_3 (
    .Input(i3), .Output(memory_cell_3_output), .Reset(Reset), .Select(n2x4_decoder_1_a2),
    .Read_Write(read_write));
  Memory_Cell memory_cell_4 (
    .Input(i3), .Output(memory_cell_4_output), .Reset(Reset), .Select(n2x4_decoder_1_a3),
    .Read_Write(read_write));
  or or_1 (a3, memory_cell_1_output, memory_cell_2_output, memory_cell_3_output, memory_cell_4_output);
  Memory_Cell memory_cell_5 (
    .Input(i2), .Output(memory_cell_5_output), .Reset(Reset), .Select(n2x4_decoder_1_a0),
    .Read_Write(read_write));
  Memory_Cell memory_cell_6 (
    .Input(i2), .Output(memory_cell_6_output), .Reset(Reset), .Select(n2x4_decoder_1_a1),
    .Read_Write(read_write));
  Memory_Cell memory_cell_7 (
    .Input(i2), .Output(memory_cell_7_output), .Reset(Reset), .Select(n2x4_decoder_1_a2),
    .Read_Write(read_write));
  Memory_Cell memory_cell_8 (
    .Input(i2), .Output(memory_cell_8_output), .Reset(Reset), .Select(n2x4_decoder_1_a3),
    .Read_Write(read_write));
  or or_2 (a2, memory_cell_5_output, memory_cell_6_output, memory_cell_7_output, memory_cell_8_output);
  Memory_Cell memory_cell_9 (
    .Input(i1), .Output(memory_cell_9_output), .Reset(Reset), .Select(n2x4_decoder_1_a0),
    .Read_Write(read_write));
  Memory_Cell memory_cell_10 (
    .Input(i1), .Output(memory_cell_10_output), .Reset(Reset), .Select(n2x4_decoder_1_a1),
    .Read_Write(read_write));
  Memory_Cell memory_cell_11 (
    .Input(i1), .Output(memory_cell_11_output), .Reset(Reset), .Select(n2x4_decoder_1_a2),
    .Read_Write(read_write));
  Memory_Cell memory_cell_12 (
    .Input(i1), .Output(memory_cell_12_output), .Reset(Reset), .Select(n2x4_decoder_1_a3),
    .Read_Write(read_write));
  or or_3 (a1, memory_cell_9_output, memory_cell_10_output, memory_cell_11_output, memory_cell_12_output);
  Memory_Cell memory_cell_13 (
    .Input(i0), .Output(memory_cell_13_output), .Reset(Reset), .Select(n2x4_decoder_1_a0),
    .Read_Write(read_write));
  Memory_Cell memory_cell_14 (
    .Input(i0), .Output(memory_cell_14_output), .Reset(Reset), .Select(n2x4_decoder_1_a1),
    .Read_Write(read_write));
  Memory_Cell memory_cell_15 (
    .Input(i0), .Output(memory_cell_15_output), .Reset(Reset), .Select(n2x4_decoder_1_a2),
    .Read_Write(read_write));
  Memory_Cell memory_cell_16 (
    .Input(i0), .Output(memory_cell_16_output), .Reset(Reset), .Select(n2x4_decoder_1_a3),
    .Read_Write(read_write));
  or or_4 (a0, memory_cell_13_output, memory_cell_14_output, memory_cell_15_output, memory_cell_16_output);
endmodule

module _8X8_Ram (
  input  [7:0] Input,
  input  a2,
  input  a1,
  input  a0,
  input  sel,
  input  r_w,
  input  rst,
  output [7:0] Output
);

  wire and_1_out, and_2_out, n4x4_ram_1_a0, n4x4_ram_1_a1, n4x4_ram_1_a2, n4x4_ram_1_a3, n4x4_ram_2_a0,
       n4x4_ram_2_a1, n4x4_ram_2_a2, n4x4_ram_2_a3, n4x4_ram_3_a0, n4x4_ram_3_a1, n4x4_ram_3_a2,
       n4x4_ram_3_a3, n4x4_ram_4_a0, n4x4_ram_4_a1, n4x4_ram_4_a2, n4x4_ram_4_a3, not_1_out;

  not not_1 (not_1_out, a2);
  and and_1 (and_1_out, sel, not_1_out);
  and and_2 (and_2_out, sel, a2);
  _4X4_Ram u_4x4_ram_1 (
    .address_1(a0), .memory_enable(a1), .read_write(and_1_out), .address_0(r_w), .a3(n4x4_ram_1_a3),
    .i0(Input[4]), .i3(Input[7]), .i2(Input[6]), .i1(Input[5]), .Reset(rst), .a2(n4x4_ram_1_a2),
    .a1(n4x4_ram_1_a1), .a0(n4x4_ram_1_a0));
  _4X4_Ram u_4x4_ram_2 (
    .address_1(a0), .memory_enable(a1), .read_write(and_2_out), .address_0(r_w), .a3(n4x4_ram_2_a3),
    .i0(Input[4]), .i3(Input[7]), .i2(Input[6]), .i1(Input[5]), .Reset(rst), .a2(n4x4_ram_2_a2),
    .a1(n4x4_ram_2_a1), .a0(n4x4_ram_2_a0));
  or or_1 (Output[7], n4x4_ram_2_a3, n4x4_ram_1_a3);
  or or_2 (Output[6], n4x4_ram_2_a2, n4x4_ram_1_a2);
  or or_3 (Output[5], n4x4_ram_2_a1, n4x4_ram_1_a1);
  or or_4 (Output[4], n4x4_ram_2_a0, n4x4_ram_1_a0);
  _4X4_Ram u_4x4_ram_3 (
    .address_1(a0), .memory_enable(a1), .read_write(and_1_out), .address_0(r_w), .a3(n4x4_ram_3_a3),
    .i0(Input[0]), .i3(Input[3]), .i2(Input[2]), .i1(Input[1]), .Reset(rst), .a2(n4x4_ram_3_a2),
    .a1(n4x4_ram_3_a1), .a0(n4x4_ram_3_a0));
  _4X4_Ram u_4x4_ram_4 (
    .address_1(a0), .memory_enable(a1), .read_write(and_2_out), .address_0(r_w), .a3(n4x4_ram_4_a3),
    .i0(Input[0]), .i3(Input[3]), .i2(Input[2]), .i1(Input[1]), .Reset(rst), .a2(n4x4_ram_4_a2),
    .a1(n4x4_ram_4_a1), .a0(n4x4_ram_4_a0));
  or or_5 (Output[3], n4x4_ram_4_a3, n4x4_ram_3_a3);
  or or_6 (Output[2], n4x4_ram_4_a2, n4x4_ram_3_a2);
  or or_7 (Output[1], n4x4_ram_4_a1, n4x4_ram_3_a1);
  or or_8 (Output[0], n4x4_ram_4_a0, n4x4_ram_3_a0);

  // Notes on the sheet:
  //   [7:4]
  //   [3:0]
endmodule

module Memory_Cell (
  input  Reset,
  input  Select,
  input  Input,
  input  Read_Write,
  output Output
);

  wire and_1_out, and_2_out, and_3_out, not_1_out, not_2_out, not_3_out, sr_latch_1_out_3;

  not not_1 (not_1_out, Reset);
  and and_1 (and_1_out, not_1_out, Input);
  not not_2 (not_2_out, and_1_out);
  and and_2 (and_2_out, and_1_out, not_3_out, Select);
  and and_3 (and_3_out, not_2_out, not_3_out, Select);
  not not_3 (not_3_out, Read_Write);
  SR_Latch sr_latch_1 (.Reset(and_3_out), .Set(and_2_out), .out_3(sr_latch_1_out_3));  // open: out_4
  and and_4 (Output, sr_latch_1_out_3, Select, Read_Write);

  // Notes on the sheet:
  //   Memory Cell
endmodule

module SR_Latch (
  input  Reset,
  input  Set,
  output out_3,
  output out_4
);

  nor nor_1 (out_3, Reset, out_4);
  nor nor_2 (out_4, out_3, Set);
endmodule

module _2X4_Decoder (
  input  i0,
  input  i1,
  input  sel,
  output a0,
  output a1,
  output a2,
  output a3
);

  wire not_1_out, not_2_out;

  not not_1 (not_1_out, i0);
  not not_2 (not_2_out, i1);
  and and_1 (a0, sel, not_2_out, not_1_out);
  and and_2 (a1, sel, not_2_out, i0);
  and and_3 (a3, sel, i1, i0);
  and and_4 (a2, sel, i1, not_1_out);
endmodule
